// Logisim project CPU_LOGISM.circ as structural Verilog
module half_adder (
  input  A,
  input  B,
  output sum,
  output carry_out
);

  xor xor_1 (sum, A, B);
  and and_1 (carry_out, A, B);
  LED led_1 (.in(sum));
  LED led_2 (.in(carry_out));
endmodule

module full_adder_1_bit (
  input  A,
  input  B,
  input  carry_in,
  output sum,
  output carry_out
);

  wire and_1_out, and_2_out, xor_1_out;

  xor xor_1 (xor_1_out, A, B);
  and and_1 (and_1_out, A, B);
  and and_2 (and_2_out, xor_1_out, carry_in);
  xor xor_2 (sum, xor_1_out, carry_in);
  or or_1 (carry_out, and_1_out, and_2_out);

  // Notes on the sheet:
  //   intermidiate_sum
  //   carry_out_1st
endmodule

module adder_2_bit (
  input  [1:0] A,
  input  carry_in,
  input  [1:0] B,
  output [1:0] sum,
  output carry_out
);

  wire full_adder_1_bit_1_carry_out;

  full_adder_1_bit full_adder_1_bit_1 (
    .A(A[0]), .B(B[0]), .carry_in(carry_in), .sum(sum[0]), .carry_out(full_adder_1_bit_1_carry_out));
  full_adder_1_bit full_adder_1_bit_2 (
    .A(A[1]), .B(B[1]), .carry_in(full_adder_1_bit_1_carry_out), .sum(sum[1]), .carry_out(carry_out));
  // Probe on sum
  LED led_1 (.in(carry_out));
endmodule

module adder_4_bit (
  input  [3:0] A,
  input  C_in,
  input  [3:0] B,
  output [3:0] sum,
  output carry_out
);

  wire adder_2_bit_1_carry_out;

  adder_2_bit adder_2_bit_1 (
    .A(A[1:0]), .carry_in(C_in), .B(B[1:0]), .sum(sum[1:0]), .carry_out(adder_2_bit_1_carry_out));
  adder_2_bit adder_2_bit_2 (
    .A(A[3:2]), .carry_in(adder_2_bit_1_carry_out), .B(B[3:2]), .sum(sum[3:2]), .carry_out(carry_out));
  // Probe on sum
endmodule

module adder_8_bit (
  input  [7:0] A,
  input  carry_in,
  input  [7:0] B,
  output [7:0] sum,
  output carry_out
);

  wire adder_4_bit_1_carry_out;

  adder_4_bit adder_4_bit_1 (
    .A(A[3:0]), .C_in(carry_in), .B(B[3:0]), .sum(sum[3:0]), .carry_out(adder_4_bit_1_carry_out));
  adder_4_bit adder_4_bit_2 (
    .A(A[7:4]), .C_in(adder_4_bit_1_carry_out), .B(B[7:4]), .sum(sum[7:4]), .carry_out(carry_out));
  // Probe on sum
endmodule

module adder_16_bit (
  input  [15:0] A,
  input  carry_in,
  input  [15:0] B,
  output [15:0] sum,
  output carry_out
);

  wire adder_8_bit_1_carry_out;

  // Probe on sum
  adder_8_bit adder_8_bit_1 (
    .A(A[7:0]), .carry_in(carry_in), .B(B[7:0]), .sum(sum[7:0]), .carry_out(adder_8_bit_1_carry_out));
  adder_8_bit adder_8_bit_2 (
    .A(A[15:8]), .carry_in(adder_8_bit_1_carry_out), .B(B[15:8]), .sum(sum[15:8]), .carry_out(carry_out));
endmodule

module adder_32_bit (
  input  [31:0] A,
  input  carry_in,
  input  [31:0] B,
  output [31:0] sum,
  output carry_out
);

  wire adder_16_bit_1_carry_out;

  // Probe on A
  // Probe on B
  adder_16_bit adder_16_bit_1 (
    .A(A[15:0]), .carry_in(carry_in), .B(B[15:0]), .sum(sum[15:0]), .carry_out(adder_16_bit_1_carry_out));
  adder_16_bit adder_16_bit_2 (
    .A(A[31:16]), .carry_in(adder_16_bit_1_carry_out), .B(B[31:16]), .sum(sum[31:16]), .carry_out(carry_out));
  // Probe on sum
endmodule

module sub_16 (
  input  [15:0] A,
  input  [15:0] B,
  input  flag,
  output [15:0] add_or_sub,
  output carry_out
);

  wire [15:0] xor_1_out;

  // Probe on A
  // Probe on B
  assign xor_1_out = B ^ {16{flag}};  // XOR_Gate xor_1, 16 bits wide
  // Probe on add_or_sub
  adder_16_bit adder_16_bit_1 (.A(A), .carry_in(flag), .B(xor_1_out), .sum(add_or_sub), .carry_out(carry_out));
endmodule

module sub_32_bit (
  input  [31:0] A,
  input  [31:0] B,
  input  inverter,
  output [31:0] sum,
  output carry_out
);

  wire [31:0] xor_1_out;

  // Probe on A
  // Probe on B
  assign xor_1_out = B ^ {32{inverter}};  // XOR_Gate xor_1, 32 bits wide
  adder_32_bit adder_32_bit_1 (.A(A), .carry_in(inverter), .B(xor_1_out), .sum(sum), .carry_out(carry_out));
  // Probe on sum
endmodule

module mutlti_8_by_1 (
  input  [7:0] A,
  input  B,
  output [7:0] out_3
);

  and and_1 (out_3[0], A[0], B);
  and and_2 (out_3[1], A[1], B);
  and and_3 (out_3[2], A[2], B);
  and and_4 (out_3[3], A[3], B);
  and and_5 (out_3[4], A[4], B);
  and and_6 (out_3[5], A[5], B);
  and and_7 (out_3[6], A[6], B);
  and and_8 (out_3[7], A[7], B);
  // Probe on out_3
endmodule

module multi_8_by_8 (
  input  [7:0] A,
  input  [7:0] B,
  output [15:0] SUM,
  output carry_out
);

  wire [7:0] mutlti_8_by_1_1_out_3, mutlti_8_by_1_2_out_3, mutlti_8_by_1_3_out_3, mutlti_8_by_1_4_out_3,
       mutlti_8_by_1_5_out_3, mutlti_8_by_1_6_out_3, mutlti_8_by_1_7_out_3, mutlti_8_by_1_8_out_3, undriven,
       undriven_2, undriven_3, undriven_4, undriven_5, undriven_6, undriven_7, undriven_8;
  wire [15:0] adder_16_bit_1_sum, adder_16_bit_2_sum, adder_16_bit_3_sum, adder_16_bit_4_sum,
       adder_16_bit_5_sum, adder_16_bit_6_sum;

  // Probe on B
  // Probe on A
  mutlti_8_by_1 mutlti_8_by_1_1 (.A(A), .B(B[0]), .out_3(mutlti_8_by_1_1_out_3));
  mutlti_8_by_1 mutlti_8_by_1_2 (.A(A), .B(B[1]), .out_3(mutlti_8_by_1_2_out_3));
  mutlti_8_by_1 mutlti_8_by_1_3 (.A(A), .B(B[2]), .out_3(mutlti_8_by_1_3_out_3));
  mutlti_8_by_1 mutlti_8_by_1_4 (.A(A), .B(B[3]), .out_3(mutlti_8_by_1_4_out_3));
  mutlti_8_by_1 mutlti_8_by_1_5 (.A(A), .B(B[4]), .out_3(mutlti_8_by_1_5_out_3));
  mutlti_8_by_1 mutlti_8_by_1_6 (.A(A), .B(B[5]), .out_3(mutlti_8_by_1_6_out_3));
  mutlti_8_by_1 mutlti_8_by_1_7 (.A(A), .B(B[6]), .out_3(mutlti_8_by_1_7_out_3));
  mutlti_8_by_1 mutlti_8_by_1_8 (.A(A), .B(B[7]), .out_3(mutlti_8_by_1_8_out_3));
  adder_16_bit adder_16_bit_1 (
    .A({undriven, mutlti_8_by_1_1_out_3}), .B({undriven_2[7:1], mutlti_8_by_1_2_out_3, undriven_2[0]}),
    .sum(adder_16_bit_1_sum));  // open: carry_in, carry_out
  adder_16_bit adder_16_bit_2 (
    .A({undriven_7[7:2], mutlti_8_by_1_3_out_3, undriven_7[1:0]}),
    .B({undriven_8[7:3], mutlti_8_by_1_4_out_3, undriven_8[2:0]}), .sum(adder_16_bit_2_sum));  // open: carry_in, carry_out
  adder_16_bit adder_16_bit_3 (
    .A({undriven_3[7:4], mutlti_8_by_1_5_out_3, undriven_3[3:0]}),
    .B({undriven_4[7:5], mutlti_8_by_1_6_out_3, undriven_4[4:0]}), .sum(adder_16_bit_3_sum));  // open: carry_in, carry_out
  adder_16_bit adder_16_bit_4 (
    .A({undriven_5[7:6], mutlti_8_by_1_7_out_3, undriven_5[5:0]}),
    .B({undriven_6[7], mutlti_8_by_1_8_out_3, undriven_6[6:0]}), .sum(adder_16_bit_4_sum));  // open: carry_in, carry_out
  adder_16_bit adder_16_bit_5 (
    .A(adder_16_bit_1_sum), .B(adder_16_bit_2_sum), .sum(adder_16_bit_5_sum));  // open: carry_in, carry_out
  adder_16_bit adder_16_bit_6 (
    .A(adder_16_bit_3_sum), .B(adder_16_bit_4_sum), .sum(adder_16_bit_6_sum));  // open: carry_in, carry_out
  // Probe on SUM
  adder_16_bit adder_16_bit_7 (
    .A(adder_16_bit_5_sum), .B(adder_16_bit_6_sum), .sum(SUM), .carry_out(carry_out));  // open: carry_in
endmodule

module multi_16_by1 (
  input  [15:0] A,
  input  B,
  output [15:0] out_3
);

  and and_1 (out_3[0], A[0], B);
  and and_2 (out_3[1], A[1], B);
  and and_3 (out_3[2], A[2], B);
  and and_4 (out_3[3], A[3], B);
  and and_5 (out_3[4], A[4], B);
  and and_6 (out_3[5], A[5], B);
  and and_7 (out_3[6], A[6], B);
  and and_8 (out_3[7], A[7], B);
  and and_9 (out_3[8], A[8], B);
  and and_10 (out_3[9], A[9], B);
  and and_11 (out_3[10], A[10], B);
  and and_12 (out_3[11], A[11], B);
  and and_13 (out_3[12], A[12], B);
  and and_14 (out_3[13], A[13], B);
  and and_15 (out_3[14], A[14], B);
  and and_16 (out_3[15], A[15], B);
  // Probe on out_3
endmodule

module multi_16_by_16 (
  input  [15:0] A,
  input  [15:0] B,
  output [31:0] SUM,
  output out_4
);

  wire [15:0] multi_16_by1_1_out_3, multi_16_by1_2_out_3, multi_16_by1_3_out_3, multi_16_by1_4_out_3,
       multi_16_by1_5_out_3, multi_16_by1_6_out_3, multi_16_by1_7_out_3, multi_16_by1_8_out_3,
       multi_16_by1_9_out_3, multi_16_by1_10_out_3, multi_16_by1_11_out_3, multi_16_by1_12_out_3,
       multi_16_by1_13_out_3, multi_16_by1_14_out_3, multi_16_by1_15_out_3, multi_16_by1_16_out_3, undriven,
       undriven_2, undriven_3, undriven_4, undriven_5, undriven_6, undriven_7, undriven_8, undriven_9,
       undriven_10, undriven_11, undriven_12, undriven_13, undriven_14, undriven_15, undriven_16;
  wire [31:0] adder_32_bit_1_sum, adder_32_bit_2_sum, adder_32_bit_3_sum, adder_32_bit_4_sum,
       adder_32_bit_5_sum, adder_32_bit_6_sum, adder_32_bit_7_sum, adder_32_bit_8_sum, adder_32_bit_9_sum,
       adder_32_bit_10_sum, adder_32_bit_11_sum, adder_32_bit_12_sum, adder_32_bit_13_sum,
       adder_32_bit_14_sum;

  // Probe on B
  // Probe on A
  multi_16_by1 multi_16_by1_1 (.A(A), .B(B[0]), .out_3(multi_16_by1_1_out_3));
  multi_16_by1 multi_16_by1_2 (.A(A), .B(B[1]), .out_3(multi_16_by1_2_out_3));
  multi_16_by1 multi_16_by1_3 (.A(A), .B(B[2]), .out_3(multi_16_by1_3_out_3));
  multi_16_by1 multi_16_by1_4 (.A(A), .B(B[3]), .out_3(multi_16_by1_4_out_3));
  multi_16_by1 multi_16_by1_5 (.A(A), .B(B[4]), .out_3(multi_16_by1_5_out_3));
  multi_16_by1 multi_16_by1_6 (.A(A), .B(B[5]), .out_3(multi_16_by1_6_out_3));
  multi_16_by1 multi_16_by1_7 (.A(A), .B(B[6]), .out_3(multi_16_by1_7_out_3));
  multi_16_by1 multi_16_by1_8 (.A(A), .B(B[7]), .out_3(multi_16_by1_8_out_3));
  multi_16_by1 multi_16_by1_9 (.A(A), .B(B[8]), .out_3(multi_16_by1_9_out_3));
  multi_16_by1 multi_16_by1_10 (.A(A), .B(B[9]), .out_3(multi_16_by1_10_out_3));
  multi_16_by1 multi_16_by1_11 (.A(A), .B(B[10]), .out_3(multi_16_by1_11_out_3));
  multi_16_by1 multi_16_by1_12 (.A(A), .B(B[11]), .out_3(multi_16_by1_12_out_3));
  multi_16_by1 multi_16_by1_13 (.A(A), .B(B[12]), .out_3(multi_16_by1_13_out_3));
  multi_16_by1 multi_16_by1_14 (.A(A), .B(B[13]), .out_3(multi_16_by1_14_out_3));
  multi_16_by1 multi_16_by1_15 (.A(A), .B(B[14]), .out_3(multi_16_by1_15_out_3));
  multi_16_by1 multi_16_by1_16 (.A(A), .B(B[15]), .out_3(multi_16_by1_16_out_3));
  adder_32_bit adder_32_bit_1 (
    .A({undriven_7, multi_16_by1_1_out_3}), .B({undriven_8[15:1], multi_16_by1_2_out_3, undriven_8[0]}),
    .sum(adder_32_bit_1_sum));  // open: carry_in, carry_out
  adder_32_bit adder_32_bit_2 (
    .A({undriven_15[15:2], multi_16_by1_3_out_3, undriven_15[1:0]}),
    .B({undriven_16[15:3], multi_16_by1_4_out_3, undriven_16[2:0]}), .sum(adder_32_bit_2_sum));  // open: carry_in, carry_out
  adder_32_bit adder_32_bit_3 (
    .A({undriven_9[15:4], multi_16_by1_5_out_3, undriven_9[3:0]}),
    .B({undriven_10[15:5], multi_16_by1_6_out_3, undriven_10[4:0]}), .sum(adder_32_bit_3_sum));  // open: carry_in, carry_out
  adder_32_bit adder_32_bit_4 (
    .A({undriven_11[15:6], multi_16_by1_7_out_3, undriven_11[5:0]}),
    .B({undriven_12[15:7], multi_16_by1_8_out_3, undriven_12[6:0]}), .sum(adder_32_bit_4_sum));  // open: carry_in, carry_out
  adder_32_bit adder_32_bit_5 (
    .A({undriven[15:8], multi_16_by1_9_out_3, undriven[7:0]}),
    .B({undriven_2[15:9], multi_16_by1_10_out_3, undriven_2[8:0]}), .sum(adder_32_bit_5_sum));  // open: carry_in, carry_out
  adder_32_bit adder_32_bit_6 (
    .A({undriven_13[15:10], multi_16_by1_11_out_3, undriven_13[9:0]}),
    .B({undriven_14[15:11], multi_16_by1_12_out_3, undriven_14[10:0]}), .sum(adder_32_bit_6_sum));  // open: carry_in, carry_out
  adder_32_bit adder_32_bit_7 (
    .A({undriven_3[15:12], multi_16_by1_13_out_3, undriven_3[11:0]}),
    .B({undriven_4[15:13], multi_16_by1_14_out_3, undriven_4[12:0]}), .sum(adder_32_bit_7_sum));  // open: carry_in, carry_out
  adder_32_bit adder_32_bit_8 (
    .A({undriven_5[15:14], multi_16_by1_15_out_3, undriven_5[13:0]}),
    .B({undriven_6[15], multi_16_by1_16_out_3, undriven_6[14:0]}), .sum(adder_32_bit_8_sum));  // open: carry_in, carry_out
  adder_32_bit adder_32_bit_9 (
    .A(adder_32_bit_7_sum), .B(adder_32_bit_8_sum), .sum(adder_32_bit_9_sum));  // open: carry_in, carry_out
  adder_32_bit adder_32_bit_10 (
    .A(adder_32_bit_1_sum), .B(adder_32_bit_2_sum), .sum(adder_32_bit_10_sum));  // open: carry_in, carry_out
  adder_32_bit adder_32_bit_11 (
    .A(adder_32_bit_3_sum), .B(adder_32_bit_4_sum), .sum(adder_32_bit_11_sum));  // open: carry_in, carry_out
  adder_32_bit adder_32_bit_12 (
    .A(adder_32_bit_5_sum), .B(adder_32_bit_6_sum), .sum(adder_32_bit_12_sum));  // open: carry_in, carry_out
  adder_32_bit adder_32_bit_13 (
    .A(adder_32_bit_10_sum), .B(adder_32_bit_11_sum), .sum(adder_32_bit_13_sum));  // open: carry_in, carry_out
  adder_32_bit adder_32_bit_14 (
    .A(adder_32_bit_12_sum), .B(adder_32_bit_9_sum), .sum(adder_32_bit_14_sum));  // open: carry_in, carry_out
  // Probe on SUM
  adder_32_bit adder_32_bit_15 (
    .A(adder_32_bit_13_sum), .B(adder_32_bit_14_sum), .sum(SUM), .carry_out(out_4));  // open: carry_in
endmodule

module comp_1 (
  input  A,
  input  B,
  output are_equal,
  output A_is_greater,
  output B_is_greater
);

  wire and_3_out, and_4_out, not_1_out, not_2_out, not_3_out, not_4_out;

  not not_1 (not_1_out, B);
  not not_2 (not_2_out, A);
  not not_3 (not_3_out, A);
  not not_4 (not_4_out, B);
  and and_1 (A_is_greater, A, not_1_out);
  and and_2 (B_is_greater, not_2_out, B);
  and and_3 (and_3_out, A, B);
  and and_4 (and_4_out, not_3_out, not_4_out);
  or or_1 (are_equal, and_3_out, and_4_out);
endmodule

module comp_2 (
  input  [1:0] A,
  input  [1:0] B,
  output is_equal,
  output A_is_greater,
  output B_is_greater
);

  wire and_1_out, and_2_out, comp_1_1_a_is_greater, comp_1_1_are_equal, comp_1_1_b_is_greater,
       comp_1_2_a_is_greater, comp_1_2_are_equal, comp_1_2_b_is_greater;

  comp_1 comp_1_1 (
    .A(A[0]), .B(B[0]), .are_equal(comp_1_1_are_equal), .A_is_greater(comp_1_1_a_is_greater),
    .B_is_greater(comp_1_1_b_is_greater));
  comp_1 comp_1_2 (
    .A(A[1]), .B(B[1]), .are_equal(comp_1_2_are_equal), .A_is_greater(comp_1_2_a_is_greater),
    .B_is_greater(comp_1_2_b_is_greater));
  and and_1 (and_1_out, comp_1_1_a_is_greater, comp_1_2_are_equal);
  and and_2 (and_2_out, comp_1_1_b_is_greater, comp_1_2_are_equal);
  and and_3 (is_equal, comp_1_1_are_equal, comp_1_2_are_equal);
  xor xor_1 (A_is_greater, comp_1_2_a_is_greater, and_1_out);
  xor xor_2 (B_is_greater, comp_1_2_b_is_greater, and_2_out);
endmodule

module comp_4_bit (
  input  [3:0] in_1,
  input  [3:0] in_2,
  output is_equal,
  output A_is_greater,
  output B_is_greater
);

  wire and_2_out, and_3_out, comp_2_1_a_is_greater, comp_2_1_b_is_greater, comp_2_1_is_equal,
       comp_2_2_a_is_greater, comp_2_2_b_is_greater, comp_2_2_is_equal;

  comp_2 comp_2_1 (
    .A(in_1[1:0]), .B(in_2[1:0]), .is_equal(comp_2_1_is_equal), .A_is_greater(comp_2_1_a_is_greater),
    .B_is_greater(comp_2_1_b_is_greater));
  comp_2 comp_2_2 (
    .A(in_1[3:2]), .B(in_2[3:2]), .is_equal(comp_2_2_is_equal), .A_is_greater(comp_2_2_a_is_greater),
    .B_is_greater(comp_2_2_b_is_greater));
  and and_1 (is_equal, comp_2_1_is_equal, comp_2_2_is_equal);
  and and_2 (and_2_out, comp_2_1_a_is_greater, comp_2_2_is_equal);
  and and_3 (and_3_out, comp_2_1_b_is_greater, comp_2_2_is_equal);
  xor xor_1 (A_is_greater, comp_2_2_a_is_greater, and_2_out);
  xor xor_2 (B_is_greater, comp_2_2_b_is_greater, and_3_out);
endmodule

module comp_8_bit (
  input  [7:0] in_1,
  input  [7:0] in_2,
  output is_equal,
  output A_is_greater,
  output B_is_greater
);

  wire and_2_out, and_3_out, comp_4_bit_1_a_is_greater, comp_4_bit_1_b_is_greater, comp_4_bit_1_is_equal,
       comp_4_bit_2_a_is_greater, comp_4_bit_2_b_is_greater, comp_4_bit_2_is_equal;

  comp_4_bit comp_4_bit_1 (
    .in_1(in_1[3:0]), .in_2(in_2[3:0]), .is_equal(comp_4_bit_1_is_equal),
    .A_is_greater(comp_4_bit_1_a_is_greater), .B_is_greater(comp_4_bit_1_b_is_greater));
  comp_4_bit comp_4_bit_2 (
    .in_1(in_1[7:4]), .in_2(in_2[7:4]), .is_equal(comp_4_bit_2_is_equal),
    .A_is_greater(comp_4_bit_2_a_is_greater), .B_is_greater(comp_4_bit_2_b_is_greater));
  and and_1 (is_equal, comp_4_bit_1_is_equal, comp_4_bit_2_is_equal);
  and and_2 (and_2_out, comp_4_bit_1_a_is_greater, comp_4_bit_2_is_equal);
  and and_3 (and_3_out, comp_4_bit_1_b_is_greater, comp_4_bit_2_is_equal);
  xor xor_1 (A_is_greater, comp_4_bit_2_a_is_greater, and_2_out);
  xor xor_2 (B_is_greater, comp_4_bit_2_b_is_greater, and_3_out);
endmodule

module comp_16_bit (
  input  [15:0] A,
  input  [15:0] B,
  output is_equal,
  output A_is_greater,
  output B_is_greater
);

  wire and_2_out, and_3_out, comp_8_bit_1_a_is_greater, comp_8_bit_1_b_is_greater, comp_8_bit_1_is_equal,
       comp_8_bit_2_a_is_greater, comp_8_bit_2_b_is_greater, comp_8_bit_2_is_equal;

  // Probe on A
  // Probe on B
  comp_8_bit comp_8_bit_1 (
    .in_1(A[7:0]), .in_2(B[7:0]), .is_equal(comp_8_bit_1_is_equal), .A_is_greater(comp_8_bit_1_a_is_greater),
    .B_is_greater(comp_8_bit_1_b_is_greater));
  comp_8_bit comp_8_bit_2 (
    .in_1(A[15:8]), .in_2(B[15:8]), .is_equal(comp_8_bit_2_is_equal),
    .A_is_greater(comp_8_bit_2_a_is_greater), .B_is_greater(comp_8_bit_2_b_is_greater));
  and and_1 (is_equal, comp_8_bit_1_is_equal, comp_8_bit_2_is_equal);
  and and_2 (and_2_out, comp_8_bit_1_a_is_greater, comp_8_bit_2_is_equal);
  and and_3 (and_3_out, comp_8_bit_1_b_is_greater, comp_8_bit_2_is_equal);
  xor xor_1 (A_is_greater, comp_8_bit_2_a_is_greater, and_2_out);
  xor xor_2 (B_is_greater, comp_8_bit_2_b_is_greater, and_3_out);
endmodule

module comp_32_bit (
  input  [31:0] A,
  input  [31:0] B,
  output is_equal,
  output A_is_greater,
  output B_is_greater
);

  wire and_2_out, and_3_out, comp_16_bit_1_a_is_greater, comp_16_bit_1_b_is_greater, comp_16_bit_1_is_equal,
       comp_16_bit_2_a_is_greater, comp_16_bit_2_b_is_greater, comp_16_bit_2_is_equal;

  // Probe on A
  // Probe on B
  comp_16_bit comp_16_bit_1 (
    .A(A[15:0]), .B(B[15:0]), .is_equal(comp_16_bit_1_is_equal), .A_is_greater(comp_16_bit_1_a_is_greater),
    .B_is_greater(comp_16_bit_1_b_is_greater));
  comp_16_bit comp_16_bit_2 (
    .A(A[31:16]), .B(B[31:16]), .is_equal(comp_16_bit_2_is_equal), .A_is_greater(comp_16_bit_2_a_is_greater),
    .B_is_greater(comp_16_bit_2_b_is_greater));
  and and_1 (is_equal, comp_16_bit_1_is_equal, comp_16_bit_2_is_equal);
  and and_2 (and_2_out, comp_16_bit_1_a_is_greater, comp_16_bit_2_is_equal);
  and and_3 (and_3_out, comp_16_bit_1_b_is_greater, comp_16_bit_2_is_equal);
  xor xor_1 (A_is_greater, comp_16_bit_2_a_is_greater, and_2_out);
  xor xor_2 (B_is_greater, comp_16_bit_2_b_is_greater, and_3_out);
endmodule

module mux_3_to_8_using_4_bit (
  input  [3:0] op_code,
  output reserved,
  output add_sub,
  output mult,
  output compare,
  output AND_op,
  output NOT_op,
  output XOR_op,
  output no_operation_or_halt
);

  wire not_1_out, not_2_out, not_3_out, not_4_out;

  not not_1 (not_1_out, op_code[0]);
  not not_2 (not_2_out, op_code[1]);
  not not_3 (not_3_out, op_code[2]);
  not not_4 (not_4_out, op_code[3]);
  and and_1 (add_sub, not_4_out, not_3_out, not_2_out, op_code[0]);
  and and_2 (mult, not_3_out, not_4_out, op_code[0], op_code[1]);
  and and_3 (compare, not_1_out, op_code[1], not_3_out, op_code[3]);
  and and_4 (AND_op, op_code[0], op_code[1], not_3_out, op_code[3]);
  and and_5 (NOT_op, op_code[0], not_2_out, op_code[2], op_code[3]);
  and and_6 (XOR_op, not_1_out, not_2_out, op_code[2], op_code[3]);
  and and_7 (no_operation_or_halt, not_1_out, op_code[3], op_code[2], op_code[3]);
  and and_8 (reserved, not_1_out, not_2_out, not_3_out, not_4_out);
endmodule

module ALU (
  input  flag,
  input  [15:0] A,
  input  [15:0] B,
  input  [3:0] in_4,
  output [15:0] over_flow,
  output [15:0] out_6
);

  wire comp_16_bit_1_a_is_greater, comp_16_bit_1_b_is_greater, comp_16_bit_1_is_equal,
       controlled_buffer_6_out, controlled_buffer_9_out, controlled_buffer_10_out,
       mux_3_to_8_using_4_bit_1_add_sub, mux_3_to_8_using_4_bit_1_and_op, mux_3_to_8_using_4_bit_1_compare,
       mux_3_to_8_using_4_bit_1_mult, mux_3_to_8_using_4_bit_1_no_operation_or_halt,
       mux_3_to_8_using_4_bit_1_not_op, mux_3_to_8_using_4_bit_1_xor_op, sub_16_1_carry_out;
  wire [7:0] bit_extender_1_out, bit_extender_2_out;
  wire [15:0] and_1_out, bit_extender_3_out, multi_8_by_8_1_sum, not_1_out, sub_16_1_add_or_sub, xor_1_out;

  // Probe on A
  // Probe on B
  Bit_Extender #(.in_width(16), .out_width(8)) bit_extender_1 (.in(A), .out(bit_extender_1_out));
  Bit_Extender #(.in_width(16), .out_width(8)) bit_extender_2 (.in(B), .out(bit_extender_2_out));
  assign and_1_out = A & B;  // AND_Gate and_1, 16 bits wide
  assign xor_1_out = A ^ B;  // XOR_Gate xor_1, 16 bits wide
  assign not_1_out = ~A;  // NOT_Gate not_1, 16 bits wide
  assign out_6 = mux_3_to_8_using_4_bit_1_and_op ? and_1_out : 16'bz;  // Controlled_Buffer controlled_buffer_1
  mux_3_to_8_using_4_bit mux_3_to_8_using_4_bit_1 (
    .op_code(in_4), .add_sub(mux_3_to_8_using_4_bit_1_add_sub), .mult(mux_3_to_8_using_4_bit_1_mult),
    .compare(mux_3_to_8_using_4_bit_1_compare), .AND_op(mux_3_to_8_using_4_bit_1_and_op),
    .NOT_op(mux_3_to_8_using_4_bit_1_not_op), .XOR_op(mux_3_to_8_using_4_bit_1_xor_op),
    .no_operation_or_halt(mux_3_to_8_using_4_bit_1_no_operation_or_halt));  // open: reserved
  sub_16 sub_16_1 (.A(A), .B(B), .flag(flag), .add_or_sub(sub_16_1_add_or_sub), .carry_out(sub_16_1_carry_out));
  assign out_6 = mux_3_to_8_using_4_bit_1_xor_op ? xor_1_out : 16'bz;  // Controlled_Buffer controlled_buffer_2
  assign out_6 = mux_3_to_8_using_4_bit_1_not_op ? not_1_out : 16'bz;  // Controlled_Buffer controlled_buffer_3
  assign out_6 = mux_3_to_8_using_4_bit_1_add_sub ? sub_16_1_add_or_sub : 16'bz;  // Controlled_Buffer controlled_buffer_4
  assign bit_extender_3_out = {{15{sub_16_1_carry_out}}, sub_16_1_carry_out};  // Bit_Extender bit_extender_3
  assign out_6 = mux_3_to_8_using_4_bit_1_mult ? multi_8_by_8_1_sum : 16'bz;  // Controlled_Buffer controlled_buffer_5
  multi_8_by_8 multi_8_by_8_1 (
    .A(bit_extender_1_out), .B(bit_extender_2_out), .SUM(multi_8_by_8_1_sum));  // open: carry_out
  comp_16_bit comp_16_bit_1 (
    .A(A), .B(B), .is_equal(comp_16_bit_1_is_equal), .A_is_greater(comp_16_bit_1_a_is_greater),
    .B_is_greater(comp_16_bit_1_b_is_greater));
  assign controlled_buffer_6_out = mux_3_to_8_using_4_bit_1_compare ? comp_16_bit_1_b_is_greater : 1'bz;  // Controlled_Buffer controlled_buffer_6
  assign out_6 = mux_3_to_8_using_4_bit_1_no_operation_or_halt ? A : 16'bz;  // Controlled_Buffer controlled_buffer_7
  assign over_flow = mux_3_to_8_using_4_bit_1_add_sub ? bit_extender_3_out : 16'bz;  // Controlled_Buffer controlled_buffer_8
  assign controlled_buffer_9_out = mux_3_to_8_using_4_bit_1_compare ? comp_16_bit_1_is_equal : 1'bz;  // Controlled_Buffer controlled_buffer_9
  assign controlled_buffer_10_out = mux_3_to_8_using_4_bit_1_compare ? comp_16_bit_1_a_is_greater : 1'bz;  // Controlled_Buffer controlled_buffer_10
  assign out_6 = controlled_buffer_9_out ? 16'h2 : 16'bz;  // Controlled_Buffer controlled_buffer_11
  assign out_6 = controlled_buffer_10_out ? 16'h4 : 16'bz;  // Controlled_Buffer controlled_buffer_12
  assign out_6 = controlled_buffer_6_out ? 16'h1 : 16'bz;  // Controlled_Buffer controlled_buffer_13
  // Probe on out_6
endmodule

module ALU_32_bit (
  input  flag,
  input  [31:0] A,
  input  [31:0] B,
  input  [3:0] in_4,
  output [31:0] over_flow,
  output [31:0] Answer
);

  wire comp_32_bit_1_a_is_greater, comp_32_bit_1_b_is_greater, comp_32_bit_1_is_equal,
       controlled_buffer_6_out, controlled_buffer_9_out, controlled_buffer_10_out,
       mux_3_to_8_using_4_bit_1_add_sub, mux_3_to_8_using_4_bit_1_and_op, mux_3_to_8_using_4_bit_1_compare,
       mux_3_to_8_using_4_bit_1_mult, mux_3_to_8_using_4_bit_1_no_operation_or_halt,
       mux_3_to_8_using_4_bit_1_not_op, mux_3_to_8_using_4_bit_1_xor_op, sub_32_bit_1_carry_out;
  wire [15:0] bit_extender_1_out, bit_extender_2_out;
  wire [31:0] and_1_out, bit_extender_3_out, multi_16_by_16_1_sum, not_1_out, sub_32_bit_1_sum, xor_1_out;

  // Probe on A
  // Probe on B
  Bit_Extender #(.in_width(32)) bit_extender_1 (.in(A), .out(bit_extender_1_out));
  Bit_Extender #(.in_width(32)) bit_extender_2 (.in(B), .out(bit_extender_2_out));
  assign and_1_out = A & B;  // AND_Gate and_1, 32 bits wide
  assign xor_1_out = A ^ B;  // XOR_Gate xor_1, 32 bits wide
  assign not_1_out = ~A;  // NOT_Gate not_1, 32 bits wide
  assign Answer = mux_3_to_8_using_4_bit_1_and_op ? and_1_out : 32'bz;  // Controlled_Buffer controlled_buffer_1
  mux_3_to_8_using_4_bit mux_3_to_8_using_4_bit_1 (
    .op_code(in_4), .add_sub(mux_3_to_8_using_4_bit_1_add_sub), .mult(mux_3_to_8_using_4_bit_1_mult),
    .compare(mux_3_to_8_using_4_bit_1_compare), .AND_op(mux_3_to_8_using_4_bit_1_and_op),
    .NOT_op(mux_3_to_8_using_4_bit_1_not_op), .XOR_op(mux_3_to_8_using_4_bit_1_xor_op),
    .no_operation_or_halt(mux_3_to_8_using_4_bit_1_no_operation_or_halt));  // open: reserved
  sub_32_bit sub_32_bit_1 (.A(A), .B(B), .inverter(flag), .sum(sub_32_bit_1_sum), .carry_out(sub_32_bit_1_carry_out));
  assign Answer = mux_3_to_8_using_4_bit_1_xor_op ? xor_1_out : 32'bz;  // Controlled_Buffer controlled_buffer_2
  assign Answer = mux_3_to_8_using_4_bit_1_not_op ? not_1_out : 32'bz;  // Controlled_Buffer controlled_buffer_3
  assign Answer = mux_3_to_8_using_4_bit_1_add_sub ? sub_32_bit_1_sum : 32'bz;  // Controlled_Buffer controlled_buffer_4
  assign bit_extender_3_out = {{31{sub_32_bit_1_carry_out}}, sub_32_bit_1_carry_out};  // Bit_Extender bit_extender_3
  assign Answer = mux_3_to_8_using_4_bit_1_mult ? multi_16_by_16_1_sum : 32'bz;  // Controlled_Buffer controlled_buffer_5
  multi_16_by_16 multi_16_by_16_1 (
    .A(bit_extender_1_out), .B(bit_extender_2_out), .SUM(multi_16_by_16_1_sum));  // open: out_4
  comp_32_bit comp_32_bit_1 (
    .A(A), .B(B), .is_equal(comp_32_bit_1_is_equal), .A_is_greater(comp_32_bit_1_a_is_greater),
    .B_is_greater(comp_32_bit_1_b_is_greater));
  assign controlled_buffer_6_out = mux_3_to_8_using_4_bit_1_compare ? comp_32_bit_1_b_is_greater : 1'bz;  // Controlled_Buffer controlled_buffer_6
  assign Answer = mux_3_to_8_using_4_bit_1_no_operation_or_halt ? A : 32'bz;  // Controlled_Buffer controlled_buffer_7
  assign over_flow = mux_3_to_8_using_4_bit_1_add_sub ? bit_extender_3_out : 32'bz;  // Controlled_Buffer controlled_buffer_8
  assign controlled_buffer_9_out = mux_3_to_8_using_4_bit_1_compare ? comp_32_bit_1_is_equal : 1'bz;  // Controlled_Buffer controlled_buffer_9
  assign controlled_buffer_10_out = mux_3_to_8_using_4_bit_1_compare ? comp_32_bit_1_a_is_greater : 1'bz;  // Controlled_Buffer controlled_buffer_10
  assign Answer = controlled_buffer_9_out ? 32'h2 : 32'bz;  // Controlled_Buffer controlled_buffer_11
  assign Answer = controlled_buffer_10_out ? 32'h4 : 32'bz;  // Controlled_Buffer controlled_buffer_12
  assign Answer = controlled_buffer_6_out ? 32'h1 : 32'bz;  // Controlled_Buffer controlled_buffer_13
  // Probe on Answer
endmodule

module instruction_splitter (
  input  [15:0] instruction_full,
  input  wrtite_enable,
  input  clock,
  output [4:0] Adress_of_B,
  output [4:0] Address_of_A,
  output [4:0] op_code,
  output flag_or_immediate
);

  Register #(.width(16)) register_1 (
    .D(instruction_full), .en(wrtite_enable), .clk(clock),
    .Q({flag_or_immediate, op_code, Address_of_A, Adress_of_B}));  // open: clr
endmodule

module matrix_multiplication (
  input  [15:0] A0,
  input  [15:0] A1,
  input  [15:0] A2,
  input  [15:0] A3,
  input  [15:0] B0,
  input  [15:0] B1,
  input  [15:0] B2,
  input  [15:0] B3,
  output [15:0] out_9,
  output [15:0] out_10,
  output [15:0] out_11,
  output [15:0] out_12
);

  wire [7:0] bit_extender_1_out, bit_extender_2_out, bit_extender_3_out, bit_extender_4_out,
       bit_extender_5_out, bit_extender_6_out, bit_extender_7_out, bit_extender_8_out;
  wire [15:0] multi_8_by_8_1_sum, multi_8_by_8_2_sum, multi_8_by_8_3_sum, multi_8_by_8_4_sum,
       multi_8_by_8_5_sum, multi_8_by_8_6_sum, multi_8_by_8_7_sum, multi_8_by_8_8_sum;

  Bit_Extender #(.in_width(16), .out_width(8)) bit_extender_1 (.in(A0), .out(bit_extender_1_out));
  Bit_Extender #(.in_width(16), .out_width(8)) bit_extender_2 (.in(A1), .out(bit_extender_2_out));
  Bit_Extender #(.in_width(16), .out_width(8)) bit_extender_3 (.in(A2), .out(bit_extender_3_out));
  Bit_Extender #(.in_width(16), .out_width(8)) bit_extender_4 (.in(A3), .out(bit_extender_4_out));
  Bit_Extender #(.in_width(16), .out_width(8)) bit_extender_5 (.in(B0), .out(bit_extender_5_out));
  Bit_Extender #(.in_width(16), .out_width(8)) bit_extender_6 (.in(B1), .out(bit_extender_6_out));
  Bit_Extender #(.in_width(16), .out_width(8)) bit_extender_7 (.in(B2), .out(bit_extender_7_out));
  Bit_Extender #(.in_width(16), .out_width(8)) bit_extender_8 (.in(B3), .out(bit_extender_8_out));
  multi_8_by_8 multi_8_by_8_1 (
    .A(bit_extender_1_out), .B(bit_extender_5_out), .SUM(multi_8_by_8_1_sum));  // open: carry_out
  multi_8_by_8 multi_8_by_8_2 (
    .A(bit_extender_2_out), .B(bit_extender_7_out), .SUM(multi_8_by_8_2_sum));  // open: carry_out
  multi_8_by_8 multi_8_by_8_3 (
    .A(bit_extender_1_out), .B(bit_extender_6_out), .SUM(multi_8_by_8_3_sum));  // open: carry_out
  multi_8_by_8 multi_8_by_8_4 (
    .A(bit_extender_2_out), .B(bit_extender_8_out), .SUM(multi_8_by_8_4_sum));  // open: carry_out
  multi_8_by_8 multi_8_by_8_5 (
    .A(bit_extender_3_out), .B(bit_extender_5_out), .SUM(multi_8_by_8_5_sum));  // open: carry_out
  multi_8_by_8 multi_8_by_8_6 (
    .A(bit_extender_4_out), .B(bit_extender_7_out), .SUM(multi_8_by_8_6_sum));  // open: carry_out
  multi_8_by_8 multi_8_by_8_7 (
    .A(bit_extender_3_out), .B(bit_extender_6_out), .SUM(multi_8_by_8_7_sum));  // open: carry_out
  multi_8_by_8 multi_8_by_8_8 (
    .A(bit_extender_4_out), .B(bit_extender_8_out), .SUM(multi_8_by_8_8_sum));  // open: carry_out
  // Probe on out_9
  adder_16_bit adder_16_bit_1 (
    .A(multi_8_by_8_1_sum), .B(multi_8_by_8_2_sum), .sum(out_9));  // open: carry_in, carry_out
  // Probe on out_10
  adder_16_bit adder_16_bit_2 (
    .A(multi_8_by_8_3_sum), .B(multi_8_by_8_4_sum), .sum(out_10));  // open: carry_in, carry_out
  // Probe on out_11
  adder_16_bit adder_16_bit_3 (
    .A(multi_8_by_8_5_sum), .B(multi_8_by_8_6_sum), .sum(out_11));  // open: carry_in, carry_out
  // Probe on out_12
  adder_16_bit adder_16_bit_4 (
    .A(multi_8_by_8_7_sum), .B(multi_8_by_8_8_sum), .sum(out_12));  // open: carry_in, carry_out
endmodule

module matrix_muliplication_32 (
  input  [31:0] A0,
  input  [31:0] A1,
  input  [31:0] A2,
  input  [31:0] A3,
  input  [31:0] B0,
  input  [31:0] B1,
  input  [31:0] B2,
  input  [31:0] B3,
  output [31:0] out_9,
  output [31:0] out_10,
  output [31:0] out_11,
  output [31:0] out_12
);

  wire [15:0] bit_extender_1_out, bit_extender_2_out, bit_extender_3_out, bit_extender_4_out,
       bit_extender_5_out, bit_extender_6_out;
  wire [31:0] multi_16_by_16_1_sum, multi_16_by_16_2_sum, multi_16_by_16_3_sum, multi_16_by_16_4_p3,
       multi_16_by_16_5_sum, multi_16_by_16_6_sum, multi_16_by_16_7_sum, multi_16_by_16_8_sum;

  Bit_Extender #(.in_width(32)) bit_extender_1 (.in(A0), .out(bit_extender_1_out));
  Bit_Extender #(.in_width(32)) bit_extender_2 (.in(A1), .out(bit_extender_2_out));
  Bit_Extender #(.in_width(32)) bit_extender_3 (.in(A2), .out(bit_extender_3_out));
  Bit_Extender #(.in_width(32)) bit_extender_4 (.in(A3), .out(bit_extender_4_out));
  Bit_Extender #(.in_width(32)) bit_extender_5 (.in(B0), .out(bit_extender_5_out));
  Bit_Extender #(.in_width(32)) bit_extender_6 (.in(B1), .out(bit_extender_6_out));
  Bit_Extender #(.in_width(32)) bit_extender_7 (.in(B2), .out(bit_extender_2_out));
  Bit_Extender #(.in_width(32)) bit_extender_8 (.in(B3), .out(bit_extender_2_out));
  multi_16_by_16 multi_16_by_16_1 (
    .A(bit_extender_1_out), .B(bit_extender_5_out), .SUM(multi_16_by_16_1_sum));  // open: out_4
  multi_16_by_16 multi_16_by_16_2 (
    .A(bit_extender_2_out), .B(bit_extender_2_out), .SUM(multi_16_by_16_2_sum));  // open: out_4
  multi_16_by_16 multi_16_by_16_3 (
    .A(bit_extender_1_out), .B(bit_extender_6_out), .SUM(multi_16_by_16_3_sum));  // open: out_4
  // multi_16_by_16 multi_16_by_16_4: pin names not known; wires that end beside it: bit_extender_2_out, bit_extender_2_out, multi_16_by_16_4_p3
  multi_16_by_16 multi_16_by_16_5 (
    .A(bit_extender_3_out), .B(bit_extender_5_out), .SUM(multi_16_by_16_5_sum));  // open: out_4
  multi_16_by_16 multi_16_by_16_6 (
    .A(bit_extender_4_out), .B(bit_extender_2_out), .SUM(multi_16_by_16_6_sum));  // open: out_4
  multi_16_by_16 multi_16_by_16_7 (
    .A(bit_extender_3_out), .B(bit_extender_6_out), .SUM(multi_16_by_16_7_sum));  // open: out_4
  multi_16_by_16 multi_16_by_16_8 (
    .A(bit_extender_4_out), .B(bit_extender_2_out), .SUM(multi_16_by_16_8_sum));  // open: out_4
  // Probe on out_9
  adder_32_bit adder_32_bit_1 (
    .A(multi_16_by_16_1_sum), .B(multi_16_by_16_2_sum), .sum(out_9));  // open: carry_in, carry_out
  // Probe on out_10
  adder_32_bit adder_32_bit_2 (
    .A(multi_16_by_16_3_sum), .B(multi_16_by_16_4_p3), .sum(out_10));  // open: carry_in, carry_out
  // Probe on out_11
  adder_32_bit adder_32_bit_3 (
    .A(multi_16_by_16_5_sum), .B(multi_16_by_16_6_sum), .sum(out_11));  // open: carry_in, carry_out
  // Probe on out_12
  adder_32_bit adder_32_bit_4 (
    .A(multi_16_by_16_7_sum), .B(multi_16_by_16_8_sum), .sum(out_12));  // open: carry_in, carry_out
endmodule

module bus_terminal (
  input  [4:0] op_code,
  input  flag,
  output move_A,
  output move_B
);

  wire not_1_out;

  and and_1 (move_A, op_code[0], op_code[1], op_code[2], op_code[3], not_1_out);
  not not_1 (not_1_out, flag);
  and and_2 (move_B, op_code[0], op_code[1], op_code[2], op_code[3], flag);
endmodule

module bus_terminal_2 (
  input  [4:0] op_code,
  input  flag,
  input  [4:0] address_A,
  input  [15:0] data,
  input  [4:0] addres_B,
  output move_A,
  output move_B,
  output move,
  output [20:0] Ram_A,
  output [20:0] Ram_B,
  output [20:0] system_ram
);

  bus_terminal bus_terminal_1 (.op_code(op_code), .flag(flag), .move_A(move_A), .move_B(move_B));
  assign Ram_A = move_A ? {data, address_A} : 21'bz;  // Controlled_Buffer controlled_buffer_1
  assign Ram_B = move_B ? {data, address_A} : 21'bz;  // Controlled_Buffer controlled_buffer_2
  or or_1 (move, move_A, move_B);

  assign system_ram = {data, addres_B};
endmodule

module bus_terminal_32_bit (
  input  [4:0] op_code,
  input  flag,
  input  [4:0] address_A,
  input  [31:0] data,
  input  [4:0] addres_B,
  output move_A,
  output move_B,
  output move,
  output [36:0] Ram_A,
  output [36:0] Ram_B,
  output [36:0] system_ram
);

  bus_terminal bus_terminal_1 (.op_code(op_code), .flag(flag), .move_A(move_A), .move_B(move_B));
  assign Ram_A = move_A ? {data, address_A} : 37'bz;  // Controlled_Buffer controlled_buffer_1
  assign Ram_B = move_B ? {data, address_A} : 37'bz;  // Controlled_Buffer controlled_buffer_2
  or or_1 (move, move_A, move_B);

  assign system_ram = {data, addres_B};
endmodule

module CPU_16 (
  input  in_1,
  input  in_2,
  input  in_3,
  input  B2,
  input  B1,
  input  A3,
  input  in_7,
  input  in_8,
  input  MAR_B,
  input  in_10,
  input  in_11,
  input  in_12,
  input  in_13,
  input  in_14,
  input  in_15,
  input  SPLITTER,
  input  in_17,
  input  MBR_A,
  input  MBR_B,
  input  in_20,
  input  in_21,
  input  in_22,
  input  in_23,
  input  in_24,
  input  in_25,
  input  in_26
);

  wire bus_terminal_2_1_move, bus_terminal_2_1_move_a, bus_terminal_2_1_move_b, clock_1_out,
       controlled_buffer_5_out, controlled_buffer_11_out, controlled_buffer_12_out,
       instruction_splitter_1_flag_or_immediate, not_1_out, not_2_out, not_3_out, not_4_out, not_5_out,
       not_6_out;
  wire [3:0] OPCODE_REGISTER_q_2, Rom_counter_q;
  wire [4:0] controlled_buffer_2_out, controlled_buffer_6_out, controlled_buffer_8_out,
       controlled_buffer_15_out, controlled_buffer_21_out, controlled_buffer_22_out,
       controlled_buffer_31_out, controlled_buffer_33_out, controlled_buffer_35_out, COUNTER_MBR_A_q,
       COUNTER_MBR_B_q, instruction_splitter_1_address_of_a, instruction_splitter_1_adress_of_b,
       instruction_splitter_1_op_code, MAR_A_q, MAR_B_q, MAR_Z_q, Program_counter_main_q;
  wire [4:4] OPCODE_REGISTER_q;
  wire [7:0] undriven;
  wire [15:0] A1_q, A2_q, A3_q, A4_q, alu_1_out_6, alu_1_over_flow, alu_register_q, B1_q, B2_q, B3_q, B4_q,
       controlled_buffer_1_out, controlled_buffer_4_out, controlled_buffer_10_out, controlled_buffer_13_out,
       controlled_buffer_15_out_2, controlled_buffer_17_out, controlled_buffer_24_out,
       controlled_buffer_25_out, INSTRUCTOIN_RAM_dout, matrix_multiplication_1_out_9,
       matrix_multiplication_1_out_10, matrix_multiplication_1_out_11, matrix_multiplication_1_out_12,
       MBR_A_q, MBR_B_q, MBR_Z_q, overflow_q, R1_q, R2_q, R3_q, R4_q, ram_1_dout, ram_2_dout, ram_3_dout;
  wire [20:0] bus_terminal_2_1_ram_a, bus_terminal_2_1_ram_b, bus_terminal_2_1_system_ram,
       controlled_buffer_16_out, controlled_buffer_19_out;
  wire [63:0] rom_1_data;

  Counter #(.max('h1f), .width(5)) Program_counter_main (
    .up(rom_1_data[6]), .count(rom_1_data[31]), .clk(clock_1_out), .Q(Program_counter_main_q));  // open: clr, load, D, carry
  // Probe on controlled_buffer_24_out
  // Probe on controlled_buffer_25_out
  Register #(.width(5)) OPCODE_REGISTER (
    .D(instruction_splitter_1_op_code), .en(rom_1_data[14]), .clk(clock_1_out),
    .Q({OPCODE_REGISTER_q[4], OPCODE_REGISTER_q_2}), .clr(rom_1_data[1]));
  // Probe on instruction_splitter_1_op_code
  Register #(.width(16)) alu_register (
    .D(alu_1_out_6), .en(rom_1_data[2]), .clk(clock_1_out), .Q(alu_register_q));  // open: clr
  ALU alu_1 (
    .flag(instruction_splitter_1_flag_or_immediate), .A(controlled_buffer_24_out),
    .B(controlled_buffer_25_out), .in_4(OPCODE_REGISTER_q_2), .over_flow(alu_1_over_flow), .out_6(alu_1_out_6));
  // Probe on alu_1_over_flow
  Register #(.width(16)) A1 (
    .D(controlled_buffer_24_out), .en(rom_1_data[13]), .clk(clock_1_out), .Q(A1_q));  // open: clr
  Register #(.width(16)) u_B1 (
    .D(controlled_buffer_25_out), .en(rom_1_data[9]), .clk(clock_1_out), .Q(B1_q));  // open: clr
  Register #(.width(16)) B3 (
    .D(controlled_buffer_25_out), .en(rom_1_data[7]), .clk(clock_1_out), .Q(B3_q));  // open: clr
  Register #(.width(16)) overflow (
    .D(alu_1_over_flow), .en(rom_1_data[35]), .clk(clock_1_out), .Q(overflow_q));  // open: clr
  Register #(.width(16)) u_A3 (
    .D(controlled_buffer_24_out), .en(rom_1_data[11]), .clk(clock_1_out), .Q(A3_q));  // open: clr
  assign controlled_buffer_1_out = not_1_out ? alu_register_q : 16'bz;  // Controlled_Buffer controlled_buffer_1
  not not_1 (not_1_out, instruction_splitter_1_flag_or_immediate);
  Register #(.width(16)) A2 (
    .D(controlled_buffer_24_out), .en(rom_1_data[12]), .clk(clock_1_out), .Q(A2_q));  // open: clr
  Register #(.width(16)) A4 (
    .D(controlled_buffer_24_out), .en(rom_1_data[10]), .clk(clock_1_out), .Q(A4_q));  // open: clr
  Register #(.width(16)) u_B2 (
    .D(controlled_buffer_25_out), .en(rom_1_data[8]), .clk(clock_1_out), .Q(B2_q));  // open: clr
  Register #(.width(16)) B4 (
    .D(controlled_buffer_25_out), .en(rom_1_data[34]), .clk(clock_1_out), .Q(B4_q));  // open: clr
  // Probe on instruction_splitter_1_address_of_a
  assign controlled_buffer_2_out = rom_1_data[56] ? instruction_splitter_1_address_of_a : 5'bz;  // Controlled_Buffer controlled_buffer_2
  assign controlled_buffer_1_out = instruction_splitter_1_flag_or_immediate ? overflow_q : 16'bz;  // Controlled_Buffer controlled_buffer_3
  assign controlled_buffer_4_out = rom_1_data[32] ? MBR_Z_q : 16'bz;  // Controlled_Buffer controlled_buffer_4
  bus_terminal_2 bus_terminal_2_1 (
    .op_code({OPCODE_REGISTER_q[4], OPCODE_REGISTER_q_2}), .flag(instruction_splitter_1_flag_or_immediate),
    .address_A(instruction_splitter_1_address_of_a), .data(controlled_buffer_4_out),
    .addres_B(instruction_splitter_1_adress_of_b), .move_A(bus_terminal_2_1_move_a),
    .move_B(bus_terminal_2_1_move_b), .move(bus_terminal_2_1_move), .Ram_A(bus_terminal_2_1_ram_a),
    .Ram_B(bus_terminal_2_1_ram_b), .system_ram(bus_terminal_2_1_system_ram));
  assign controlled_buffer_5_out = rom_1_data[32] ? bus_terminal_2_1_move_a : 1'bz;  // Controlled_Buffer controlled_buffer_5
  assign controlled_buffer_6_out = rom_1_data[61] ? COUNTER_MBR_A_q : 5'bz;  // Controlled_Buffer controlled_buffer_6
  Register #(.width(5)) MAR_Z (
    .D(controlled_buffer_6_out), .en(rom_1_data[17]), .clk(clock_1_out), .Q(MAR_Z_q));  // open: clr
  assign controlled_buffer_6_out = rom_1_data[58] ? Program_counter_main_q : 5'bz;  // Controlled_Buffer controlled_buffer_7
  Register #(.width(5)) MAR_A (
    .D(controlled_buffer_8_out), .en(rom_1_data[16]), .clk(clock_1_out), .Q(MAR_A_q));  // open: clr
  assign controlled_buffer_8_out = rom_1_data[60] ? COUNTER_MBR_A_q : 5'bz;  // Controlled_Buffer controlled_buffer_8
  assign controlled_buffer_8_out = rom_1_data[54] ? instruction_splitter_1_address_of_a : 5'bz;  // Controlled_Buffer controlled_buffer_9
  assign controlled_buffer_10_out = rom_1_data[5] ? controlled_buffer_1_out : 16'bz;  // Controlled_Buffer controlled_buffer_10
  assign controlled_buffer_11_out = rom_1_data[32] ? bus_terminal_2_1_move_b : 1'bz;  // Controlled_Buffer controlled_buffer_11
  assign controlled_buffer_12_out = rom_1_data[32] ? bus_terminal_2_1_move : 1'bz;  // Controlled_Buffer controlled_buffer_12
  // Probe on instruction_splitter_1_adress_of_b
  instruction_splitter instruction_splitter_1 (
    .instruction_full(MBR_Z_q), .wrtite_enable(rom_1_data[26]), .clock(clock_1_out),
    .Adress_of_B(instruction_splitter_1_adress_of_b), .Address_of_A(instruction_splitter_1_address_of_a),
    .op_code(instruction_splitter_1_op_code), .flag_or_immediate(instruction_splitter_1_flag_or_immediate));
  assign controlled_buffer_13_out = rom_1_data[32] ? ram_2_dout : 16'bz;  // Controlled_Buffer controlled_buffer_13
  assign controlled_buffer_13_out = rom_1_data[5] ? INSTRUCTOIN_RAM_dout : 16'bz;  // Controlled_Buffer controlled_buffer_14
  not not_2 (not_2_out, controlled_buffer_5_out);
  Pull_Resistor pull_resistor_1 (.node(controlled_buffer_5_out));
  Pull_Resistor pull_resistor_2 (.node(controlled_buffer_12_out));
  assign {controlled_buffer_15_out_2, controlled_buffer_15_out} = rom_1_data[32] ? bus_terminal_2_1_ram_a : 21'bz;  // Controlled_Buffer controlled_buffer_15
  assign controlled_buffer_16_out = rom_1_data[32] ? bus_terminal_2_1_ram_b : 21'bz;  // Controlled_Buffer controlled_buffer_16
  Register #(.width(16)) MBR_Z (
    .D(controlled_buffer_13_out), .en(rom_1_data[27]), .clk(clock_1_out), .Q(MBR_Z_q));  // open: clr
  assign controlled_buffer_17_out = not_2_out ? ram_1_dout : 16'bz;  // Controlled_Buffer controlled_buffer_17
  Register #(.width(16)) u_MBR_A (
    .D(controlled_buffer_17_out), .en(rom_1_data[28]), .clk(clock_1_out), .Q(MBR_A_q),
    .clr(controlled_buffer_11_out));
  not not_3 (not_3_out, controlled_buffer_11_out);
  assign controlled_buffer_17_out = controlled_buffer_5_out ? controlled_buffer_15_out_2 : 16'bz;  // Controlled_Buffer controlled_buffer_18
  Pull_Resistor pull_resistor_3 (.node(controlled_buffer_11_out));
  Pull_Resistor pull_resistor_4 (.node({controlled_buffer_15_out_2, controlled_buffer_15_out}));
  Pull_Resistor pull_resistor_5 (.node(controlled_buffer_16_out));
  assign controlled_buffer_19_out = rom_1_data[32] ? bus_terminal_2_1_system_ram : 21'bz;  // Controlled_Buffer controlled_buffer_19
  Counter #(.max('h1f), .width(5)) COUNTER_MBR_A (
    .load(rom_1_data[50]), .up(1'b1), .count(rom_1_data[51]), .clk(clock_1_out), .D(controlled_buffer_2_out),
    .Q(COUNTER_MBR_A_q));  // open: clr, carry
  Register #(.width(16)) u_MBR_B (
    .D(controlled_buffer_16_out[20:5]), .en(rom_1_data[29]), .clk(clock_1_out), .Q(MBR_B_q),
    .clr(controlled_buffer_5_out));
  assign controlled_buffer_16_out[20:5] = not_3_out ? ram_3_dout : 16'bz;  // Controlled_Buffer controlled_buffer_20
  Pull_Resistor pull_resistor_6 (.node(controlled_buffer_19_out));
  Clock clock_1 (.out(clock_1_out));
  assign controlled_buffer_21_out = rom_1_data[55] ? instruction_splitter_1_adress_of_b : 5'bz;  // Controlled_Buffer controlled_buffer_21
  assign controlled_buffer_22_out = rom_1_data[59] ? COUNTER_MBR_B_q : 5'bz;  // Controlled_Buffer controlled_buffer_22
  assign controlled_buffer_22_out = rom_1_data[30] ? instruction_splitter_1_adress_of_b : 5'bz;  // Controlled_Buffer controlled_buffer_23
  Register #(.width(16)) R1 (
    .D(matrix_multiplication_1_out_9), .en(rom_1_data[36]), .clk(clock_1_out), .Q(R1_q));  // open: clr
  Register #(.width(16)) R2 (
    .D(matrix_multiplication_1_out_10), .en(rom_1_data[37]), .clk(clock_1_out), .Q(R2_q));  // open: clr
  Register #(.width(16)) R3 (
    .D(matrix_multiplication_1_out_11), .en(rom_1_data[38]), .clk(clock_1_out), .Q(R3_q));  // open: clr
  matrix_multiplication matrix_multiplication_1 (
    .A0(A1_q), .A1(A2_q), .A2(A3_q), .A3(A4_q), .B0(B1_q), .B1(B2_q), .B2(B3_q), .B3(B4_q),
    .out_9(matrix_multiplication_1_out_9), .out_10(matrix_multiplication_1_out_10),
    .out_11(matrix_multiplication_1_out_11), .out_12(matrix_multiplication_1_out_12));
  Register #(.width(16)) R4 (
    .D(matrix_multiplication_1_out_12), .en(rom_1_data[39]), .clk(clock_1_out), .Q(R4_q));  // open: clr
  assign controlled_buffer_24_out = rom_1_data[4] ? MBR_A_q : 16'bz;  // Controlled_Buffer controlled_buffer_24
  assign controlled_buffer_25_out = rom_1_data[3] ? MBR_B_q : 16'bz;  // Controlled_Buffer controlled_buffer_25
  Register #(.width(5)) u_MAR_B (
    .D(controlled_buffer_22_out), .en(rom_1_data[15]), .clk(clock_1_out), .Q(MAR_B_q));  // open: clr
  assign controlled_buffer_13_out = rom_1_data[40] ? R1_q : 16'bz;  // Controlled_Buffer controlled_buffer_26
  assign controlled_buffer_13_out = rom_1_data[41] ? R2_q : 16'bz;  // Controlled_Buffer controlled_buffer_27
  assign controlled_buffer_13_out = rom_1_data[42] ? R3_q : 16'bz;  // Controlled_Buffer controlled_buffer_28
  assign controlled_buffer_13_out = rom_1_data[43] ? R4_q : 16'bz;  // Controlled_Buffer controlled_buffer_29
  Counter #(.max('h1f), .width(5)) COUNTER_MBR_B (
    .load(rom_1_data[52]), .up(1'b1), .count(rom_1_data[53]), .clk(clock_1_out),
    .D(controlled_buffer_21_out), .Q(COUNTER_MBR_B_q));  // open: clr, carry
  assign controlled_buffer_10_out = rom_1_data[57] ? MBR_Z_q : 16'bz;  // Controlled_Buffer controlled_buffer_30
  assign controlled_buffer_31_out = not_4_out ? MAR_A_q : 5'bz;  // Controlled_Buffer controlled_buffer_31
  not not_4 (not_4_out, controlled_buffer_5_out);
  assign controlled_buffer_31_out = rom_1_data[32] ? controlled_buffer_15_out : 5'bz;  // Controlled_Buffer controlled_buffer_32
  RAM #(.addrWidth(5), .dataWidth(16)) INSTRUCTOIN_RAM (
    .addr(MAR_Z_q), .we(rom_1_data[25]), .oe(rom_1_data[24]), .clk(clock_1_out), .dout(INSTRUCTOIN_RAM_dout));  // open: din
  RAM #(.addrWidth(5), .dataWidth(16)) ram_1 (
    .addr(controlled_buffer_31_out), .we(rom_1_data[23]), .oe(rom_1_data[22]), .clk(clock_1_out),
    .din(controlled_buffer_24_out), .dout(ram_1_dout));
  // Probe on INSTRUCTOIN_RAM_dout
  assign controlled_buffer_33_out = not_5_out ? MAR_Z_q : 5'bz;  // Controlled_Buffer controlled_buffer_33
  not not_5 (not_5_out, controlled_buffer_12_out);
  // Probe on controlled_buffer_10_out
  // Probe on ram_1_dout
  assign controlled_buffer_33_out = rom_1_data[32] ? controlled_buffer_19_out[4:0] : 5'bz;  // Controlled_Buffer controlled_buffer_34
  assign controlled_buffer_35_out = not_6_out ? MAR_B_q : 5'bz;  // Controlled_Buffer controlled_buffer_35
  not not_6 (not_6_out, controlled_buffer_11_out);
  assign controlled_buffer_35_out = rom_1_data[32] ? controlled_buffer_16_out[4:0] : 5'bz;  // Controlled_Buffer controlled_buffer_36
  RAM #(.addrWidth(5), .dataWidth(16)) ram_2 (
    .addr(controlled_buffer_33_out), .we(rom_1_data[21]), .oe(rom_1_data[20]), .clk(clock_1_out),
    .din(controlled_buffer_10_out), .dout(ram_2_dout));
  RAM #(.addrWidth(5), .dataWidth(16)) ram_3 (
    .addr(controlled_buffer_35_out), .we(rom_1_data[19]), .oe(rom_1_data[18]), .clk(clock_1_out),
    .din(controlled_buffer_25_out), .dout(ram_3_dout));
  // Probe on ram_3_dout
  Counter #(.max('hf), .width(4)) Rom_counter (
    .clr(rom_1_data[0]), .count(1'b1), .clk(clock_1_out), .Q(Rom_counter_q));  // open: load, up, D, carry
  ROM #(.dataWidth(64)) rom_1 (.addr({OPCODE_REGISTER_q_2, Rom_counter_q}), .data(rom_1_data));
  Counter #(.max('h1f), .width(5)) Program_Counter ();  // open: clr, load, up, count, clk, D, carry, Q
  Counter #(.max('h1f), .width(5)) MBR_A_Counter ();  // open: clr, load, up, count, clk, D, carry, Q
  instruction_splitter instruction_splitter_2 ();  // open: instruction_full, wrtite_enable, clock, Adress_of_B, Address_of_A, op_code, flag_or_immediate
  Counter #(.max('h1f), .width(5)) MBR_B_Counter ();  // open: clr, load, up, count, clk, D, carry, Q
  matrix_multiplication matrix_multiplication_2 ();  // open: A0, A1, A2, A3, B0, B1, B2, B3, out_9, out_10, out_11, out_12
  RAM #(.dataWidth(16)) Instruction_RAM ();  // open: addr, we, oe, clk, din, dout
  RAM #(.dataWidth(16)) ram_4 ();  // open: addr, we, oe, clk, din, dout
  RAM #(.dataWidth(16)) ram_5 ();  // open: addr, we, oe, clk, din, dout
  RAM #(.dataWidth(16)) ram_6 ();  // open: addr, we, oe, clk, din, dout
  ROM #(.dataWidth(64)) rom_2 (.addr(undriven));  // open: data
  Counter #(.max('h1f), .width(5)) PCU_part ();  // open: clr, load, up, count, clk, D, carry, Q

  // Notes on the sheet:
  //   __
  //   __
  //   __
  //   __
  //   __
  //   __
  //   __
  //   __
  //   __
  //   __
  //   __
  //   __
  //   __
  //   __
  //   __
  //   __
  //   __
  //   __
  //   __
  //   __
  //   __
  //   __
  //   __
  //   __
  //   __
  //   __
  //   __
  //   __
  //   __
  //   __
  //   __
  //   __
  //   __
  //   __
  //   __
  //   __
  //   __
  //   __
  //   __
  //   __
  //   __
  //   __
  //   __
  //   __
  //   __
  //   __
  //   __
  //   __
  //   __
  //   __
  //   __
  //   __
  //   __
  //   __
  //   __
  //   __
  //   __
  //   __
  //   __
  //   __
  //   __
  //   __
  //   __
  //   __
  //   __
  //   __
  //   __
  //   __
  //   __
  //   __
  //   __
  //   __
  //   __
  //   __
  //   __
  //   __
  //   __
  //   __
  //   __
  //   __
  //   __
  //   __
  //   __
  //   __
  //   __
  //   __
  //   __
  //   __
  //   __
  //   __
  //   __
  //   __
  //   __
  //   __
  //   __
  //   __
  //   __
  //   __
  //   __
  //   __
  //   __
  //   __
  //   __
  //   __
  //   __
  //   __
  //   __
  //   __
  //   __
  //   __
  //   __
  //   __
  //   __
  //   __
  //   __
  //   __
  //   __
  //   __
  //   __
  //   __
  //   __
  //   __
  //   __
  //   __
  //   __
  //   __
  //   __
  //   __
  //   __
  //   __
  //   __
  //   __
  //   __
  //   __
  //   __
  //   __
  //   __
  //   __
  //   __
  //   __
  //   __
  //   __
  //   __
  //   __
  //   __
  //   __
  //   __
  //   __
  //   __
  //   __
  //   __
  //   __
  //   __
  //   __
  //   __
  //   __
  //   __
  //   __
  //   __
  //   __
  //   __
  //   __
  //   __
  //   __
  //   __
  //   __
  //   __
  //   __
  //   __
  //   __
  //   __
  //   __
  //   __
  //   __
  //   __
  //   __
  //   __
  //   __
  //   __
  //   __
  //   __
  //   __
  //   __
  //   __
  //   __
  //   __
  //   __
  //   __
  //   __
  //   __
  //   __
  //   __
  //   __
  //   __
  //   __
  //   __
  //   __
  //   __
  //   __
  //   __
  //   __
  //   __
  //   __
  //   __
  //   __
  //   __
  //   __
  //   __________
  //   __________
  //   __
  //   __
  //   __
  //   __
  //   __
  //   __
  //   __
  //   __
  //   __
  //   __
  //   __
  //   __
  //   __
  //   __
  //   __
  //   __
  //   __
  //   __
  //   __
  //   __
  //   __
  //   __
  //   __
  //   __
  //   __
  //   __
  //   __
  //   __
  //   __
  //   __
  //   __
  //   __
  //   __
  //   __
  //   __
  //   __
  //   __
  //   __
  //   __
  //   __
  //   __
  //   __
  //   __
  //   __
  //   __
  //   __
  //   __
  //   __
  //   __
  //   __
  //   __
  //   __
  //   __
  //   __
  //   __
  //   __
  //   __
  //   __
  //   __
  //   __
  //   __
  //   __
  //   __
  //   __
  //   __
  //   __
  //   __
  //   __
  //   __
  //   __
  //   __
  //   __
  //   __
  //   __
  //   __
  //   __
  //   __
  //   __
  //   __
  //   __
  //   __
  //   __
  //   __
  //   __
  //   __
  //   __
  //   __
  //   __
  //   __
  //   __
  //   __
  //   __
  //   __
  //   __
  //   __
  //   __
  //   __
  //   __
  //   __
  //   __
  //   __
  //   __
  //   __
  //   __
  //   __
  //   __
  //   __
  //   __
  //   __
  //   __
  //   __
  //   __
  //   __
  //   __
  //   __
  //   __
  //   __
  //   __
  //   __
  //   __
  //   __
  //   __
  //   __
  //   __
  //   __
  //   __
  //   __
  //   __
  //   __
  //   __
  //   __
  //   __
  //   __
  //   __
  //   __
  //   __
  //   __
  //   __
  //   __
  //   __
  //   __
  //   __
  //   __
  //   __
  //   __
  //   __
  //   __
  //   __
  //   __
  //   __
  //   __
  //   __
  //   __
  //   __
  //   __
  //   __
  //   __
  //   __
  //   __
  //   __
  //   __
  //   __
  //   __
  //   __
  //   __
  //   __
  //   __
  //   __
  //   __
  //   __
  //   __
  //   __
  //   __
  //   __
  //   __
  //   __
  //   __
  //   __
  //   __
  //   __
  //   __
  //   __
  //   __
  //   __
  //   __
  //   __
  //   __
  //   __
  //   __
  //   __
  //   __
  //   __
  //   __
  //   __
  //   __
  //   __
  //   __
  //   __
  //   __
  //   __
  //   __
  //   __
  //   __
  //   __
  //   __
  //   __
  //   __
  //   __
  //   __
  //   __
  //   __
  //   __
  //   __
  //   __
  //   __
  //   __
  //   __
  //   __
  //   __
  //   __
  //   __
  //   __
  //   __
  //   __
  //   __
  //   __
  //   __
  //   __
  //   __
  //   __
  //   __
  //   __
  //   __
  //   __
  //   __
  //   __
  //   __
  //   __
  //   __
  //   __
  //   __
  //   __
  //   __
  //   __
  //   __
  //   __
  //   __
  //   __
  //   __
  //   __
  //   __
  //   __
  //   __
  //   __
  //   __
  //   __
  //   __
  //   __
  //   __
  //   __
  //   __
  //   __
  //   __
  //   __
  //   __
  //   __
  //   __
  //   __
  //   __
  //   __
  //   __
  //   __
  //   __
  //   __
  //   __
  //   __
  //   __
  //   __
  //   __
  //   __
  //   __
  //   __
  //   __
  //   __
  //   __
  //   __
  //   __
  //   __
  //   __
  //   __
  //   __
  //   __
  //   __
  //   __
  //   __
  //   __
  //   __
  //   __
  //   __
  //   __
  //   __
  //   __
  //   __
  //   __
  //   __
  //   __
  //   __
  //   __
  //   __
  //   __
  //   __
  //   __
  //   __
  //   __
  //   __
  //   __
  //   __
  //   __
  //   __
  //   __
  //   __
  //   __
  //   __
  //   __
  //   __
  //   __
  //   __
  //   __
  //   __
  //   __
  //   __
  //   __
  //   __
  //   __
  //   __
  //   __
  //   __
  //   __
  //   __
  //   __
  //   __
  //   __
  //   __
  //   __
  //   __
  //   __
  //   __
  //   __
  //   __
  //   __
  //   __
  //   __
  //   __
  //   __
  //   __
  //   __
  //   __
  //   __
  //   __
  //   __
  //   __
  //   __
  //   __
  //   __
  //   __
  //   __
  //   __
  //   __
  //   __
  //   __
  //   __
  //   __
  //   __
  //   __
  //   __
  //   __
  //   __
  //   __
  //   __
  //   __
  //   __
  //   __
  //   __
  //   __
  //   __
  //   __
  //   __
  //   __
  //   __
  //   __
  //   __
  //   __
  //   __
  //   __
  //   __
  //   __
  //   __
  //   __
  //   __
  //   __
  //   __
  //   __
  //   __
  //   __
  //   __
  //   __
  //   __
  //   __
  //   __
  //   __
  //   __
  //   __
  //   __
  //   __
  //   __
  //   __
  //   __
  //   __
  //   __
  //   __
  //   __
  //   __
  //   __
  //   __
  //   __
  //   __
  //   __
  //   __
  //   __
  //   __
  //   __
  //   __
  //   __
  //   __
  //   __
  //   __
  //   __
  //   __
  //   __
  //   __
  //   __
  //   __
  //   __
  //   __
  //   __
  //   __
  //   __
  //   __
  //   __
  //   __
  //   __
  //   __
  //   __
  //   __
  //   __
  //   __
  //   __
  //   __
  //   __
  //   __
  //   __
  //   __
  //   __
  //   __
  //   __
  //   __
  //   __
  //   __
  //   __
  //   __
  //   __
  //   __
  //   __
  //   __
  //   __
  //   __
  //   __
  //   __
  //   __
  //   __
  //   __
  //   __
  //   __
  //   __
  //   __
  //   __
  //   __
  //   __
  //   __
  //   __
  //   __
  //   __
  //   __
  //   __
  //   __
  //   __
  //   __
  //   __
  //   __
  //   __
  //   __
  //   __
  //   __
  //   __
  //   __
  //   __
  //   __
  //   __
  //   __
  //   __
  //   __
  //   __
  //   __
  //   __
  //   __
  //   __
  //   __
  //   __
  //   __
  //   __
  //   __
  //   __
  //   __
  //   __
  //   __
  //   __
  //   __
  //   __
  //   __
  //   __
  //   __
  //   __
  //   __
  //   __
  //   __
  //   __
  //   __
  //   __
  //   __
  //   __
  //   __
  //   __
  //   __
  //   __
  //   __
  //   __
  //   __
  //   __
  //   __
  //   __
  //   __
  //   __
  //   __
  //   __
  //   __
  //   __
  //   __
  //   __
  //   __
  //   __
  //   __
  //   __
  //   __
  //   __
  //   __
  //   __
  //   __
  //   __
  //   __
  //   __
  //   __
  //   __
  //   __
  //   __
  //   __
  //   __
  //   __
  //   __
  //   __
  //   __
  //   __
  //   __
  //   __
  //   __
  //   __
  //   __
  //   __
  //   __
  //   __
  //   __
  //   __
  //   __
  //   __
  //   __
  //   __
  //   __
  //   __
  //   __
  //   __
  //   __
  //   __
  //   __
  //   __
  //   __
  //   __
  //   __
  //   __
  //   __
  //   __
  //   __
  //   __
  //   __
  //   __
  //   __
  //   __
  //   __
  //   __
  //   __
  //   __
  //   __
  //   __
  //   __
  //   __
  //   __
  //   __
  //   __
  //   __
  //   __
  //   __
  //   __
  //   __
  //   __
  //   __
  //   __
  //   __
  //   __
  //   __
  //   __
  //   __
  //   __
  //   __
  //   __
  //   __
  //   __
  //   __
  //   __
  //   __
  //   __
  //   __
  //   __
  //   __
  //   __
  //   __
  //   __
  //   __
  //   __
  //   __
  //   __
  //   O
  //   __
  //   __
  //   __
  //   __
  //   __
  //   __
  //   __
  //   __
  //   __
  //   __
  //   __
  //   __
  //   __
  //   __
  //   __
  //   __
  //   __
  //   __
  //   __
  //   __
  //   __
  //   __
  //   __
  //   __
  //   __
  //   __
  //   __
  //   __
  //   __
  //   __
  //   __
  //   __
  //   __
  //   __
  //   __
  //   __
  //   __
  //   __
  //   __
  //   __
  //   __
  //   __
  //   __
  //   __
  //   __
  //   __
  //   __
  //   __
  //   __
  //   __
  //   __
  //   __
  //   __
  //   __
  //   __
  //   __
  //   __
  //   __
  //   __
  //   __
  //   __
  //   __
  //   __
  //   __
  //   __
  //   __
  //   __
  //   __
  //   __
  //   __
  //   __
  //   __
  //   __
  //   __
  //   __
  //   __
  //   __
  //   __
  //   __
  //   __
  //   __
  //   __
  //   __
  //   __
  //   __
  //   __
  //   __
  //   __
  //   __
  //   __
  //   __
  //   __
  //   __
  //   __
  //   __
  //   __
  //   __
  //   __
  //   __
  //   __
  //   __
  //   __
  //   __
  //   __
  //   __
  //   __
  //   __
  //   __
  //   __
  //   __
  //   __
  //   __
  //   __
  //   __
  //   __
  //   __
  //   __
  //   __
  //   __
  //   __
  //   __
  //   __
  //   __
  //   __
  //   __
  //   __
  //   __
  //   __
  //   __
  //   __
  //   __
  //   __
  //   __
  //   __
  //   __
  //   __
  //   __
  //   __
  //   __
  //   __
  //   __
  //   __
  //   __
  //   __
  //   __
  //   __
  //   __
  //   __
  //   __
  //   __
  //   __
  //   __
  //   __
  //   __
  //   __
  //   __
  //   __
  //   __
  //   __
  //   __
  //   __
  //   __
  //   __
  //   __
  //   __
  //   __
  //   __
  //   __
  //   __
  //   __
  //   __
  //   __
  //   __
  //   __
  //   __
  //   __
  //   __
  //   __
  //   __
  //   __
  //   __
  //   __
  //   __
  //   __
  //   __
  //   __
  //   __
  //   __
  //   __
  //   __
  //   __
  //   __
  //   __
  //   __
  //   __
  //   __
  //   __
  //   __
  //   __
  //   __
  //   __
  //   __
  //   __
  //   __
  //   __
  //   __
  //   __
  //   __
  //   __
  //   __
  //   __
  //   __
  //   __
  //   __
  //   __
  //   __
  //   __
  //   __
  //   __
  //   __
  //   __
  //   __
  //   __
  //   __
  //   __
  //   __
  //   __
  //   __
  //   __
  //   __
  //   __
  //   __
  //   __
  //   __
  //   __
  //   __
  //   __
  //   __
  //   __
  //   __
  //   __
  //   __
  //   __
  //   __
  //   __
  //   __
  //   __
  //   __
  //   __
  //   __
  //   __
  //   __
  //   __
  //   __
  //   __
  //   __
  //   __
  //   __
  //   __
  //   __
  //   __
  //   __
  //   __
  //   __
  //   __
  //   __
  //   __
  //   __
  //   __
  //   __
  //   __
  //   __
  //   __
  //   __
  //   __
  //   __
  //   __
  //   __
  //   __
  //   __
  //   __
  //   __
  //   __
  //   __
  //   __
  //   __
  //   __
  //   __
  //   __
  //   __
  //   __
  //   __
  //   __
  //   __
  //   __
  //   __
  //   __
  //   __
  //   __
  //   __
  //   __
  //   __
  //   __
  //   __
  //   __
  //   __
  //   __
  //   __
  //   __
  //   __
  //   __
  //   __
  //   __
  //   __
  //   __
  //   __
  //   __
  //   __
  //   __
  //   __
  //   __
  //   __
  //   __
  //   __
  //   __
  //   __
  //   __
  //   __
  //   __
  //   __
  //   __
  //   __
  //   __
  //   __
  //   __
  //   __
  //   __
  //   __
  //   __
  //   __
  //   __
  //   __
  //   __
  //   __
  //   __
  //   __
  //   __
  //   __
  //   __
  //   __
  //   __
  //   __
  //   __
  //   __
  //   __
  //   __
  //   __
  //   __
  //   __
  //   __
  //   __
  //   __
  //   __
  //   __
  //   __
  //   __
  //   __
  //   __
  //   __
  //   __
  //   __
  //   __
  //   __
  //   __
  //   __
  //   __
  //   __
  //   __
  //   __
  //   __
  //   __
  //   __
  //   __
  //   __
  //   __
  //   __
  //   __
  //   __
  //   __
  //   __
  //   __
  //   __
  //   __
  //   __
  //   __
  //   __
  //   __
  //   __
  //   __
  //   __
  //   __
  //   __
  //   __
  //   __
  //   __
  //   __
  //   __
  //   __
  //   __
  //   __
  //   __
  //   __
  //   __
  //   __
  //   __
  //   __
  //   __
  //   __
  //   __
  //   __
  //   __
  //   __
  //   __
  //   __
  //   __
  //   __
  //   __
  //   __
  //   __
  //   __
  //   __
  //   __
  //   __
  //   __
  //   __
  //   __
  //   __
  //   __
  //   __
  //   __
  //   __
  //   __
  //   __
  //   __
  //   __
  //   __
  //   __
  //   __
  //   __
  //   __
  //   __
  //   __
  //   __
  //   __
  //   __
  //   __
  //   __
  //   __
  //   __
  //   __
  //   __
  //   __
  //   __
  //   __
  //   __
  //   __
  //   __
  //   __
  //   __
  //   __
  //   __
  //   __
  //   __
  //   __
  //   __
  //   __
  //   __
  //   __
  //   __
  //   __
  //   __
  //   __
  //   __
  //   __
  //   __
  //   __
  //   __
  //   __
  //   __
  //   __
  //   __
  //   __
  //   __
  //   __
  //   __
  //   __
  //   __
  //   __
  //   __
  //   __
  //   __
  //   __
  //   __
  //   __
  //   __
  //   __
  //   __
  //   __
  //   __
  //   __
  //   __
  //   __
  //   __
  //   __
  //   __
  //   __
  //   __
  //   __
  //   __
  //   __
  //   __
  //   __
  //   __
  //   __
  //   __
  //   __
  //   __
  //   __
  //   __
  //   __
  //   __
  //   __
  //   __
  //   __
  //   __
  //   __
  //   __
  //   __
  //   __
  //   __
  //   __
  //   __
  //   __
  //   __
  //   __
  //   __
  //   __
  //   __
  //   __
  //   __
  //   __
  //   __
  //   __
  //   __
  //   __
  //   __
  //   __
  //   __
  //   __
  //   MBR_A_COUNTER_G5
  //   MBR-B-COUNTER-LOAD
  //   MBR_A_COUNTER_LOAD
  //   MBR-B-COUNTER-G5
  //   MAR_A_ADD-BUFFER
  //   COUNTERb_BUFFER
  //   COUNTERa_BUFFER
  //   system_buffer-we
  //   COUNTER_RESET
  //   OPCODE_RESET
  //   alu rigister
  //   MBR-B_BUFFER
  //   MBR_A_BUFFER
  //   mbrZ_splitter-buffer
  //   pc_we
  //   B3
  //   A4
  //   A2
  //   A1
  //   OP_REGISTER
  //   MAR_A_WE
  //   MAR_Z_WE
  //   RAM_B_OE
  //   RAM_B_WE
  //   SYSTEM_RAM_OE
  //   SYSTEM_RAM_WE
  //   RAM_A_OE
  //   RAM_A_WE
  //   INSTRUCTION_RAM_OE
  //   INSTRUCTION_RAM_WE
  //   MBR_Z
  //   MAR_B_ADD_BUFFER
  //   R2
  //   R3
  //   R4
  //   R1_BUFFER
  //   R2_BUFFER
  //   R3_BUFFER
  //   R4-BUFFER
  //   A1_BUFFER
  //   A2_BUFFER
  //   A3_BUFFER
  //   B1_BUFFER
  //   B2_BUFFER
  //   B3_BUFFER
  //   MARZ-BUFFER
  //   COUNTER+MAR+A
  //   COUNTER+MAR+B
  //   STORE-MARZ-BUFFER
  //   Instruction_RAM
  //   RAM_A
  //   COUNTER_G5
  //   terminal-buffer-on
  //   A4_BUFFER
  //   b4
  //   store_oveflow
  //   R1
  //   System_RAM
  //   RAM_B
  //   contents of rom_1 (hex, n*v repeats v):
  //   400000001020000 8000020 4018020 4000 16*0 40000040018000 440000 30000000 80000001c 88000005c
  //   400000000020000 3 25*0 40000040018000 80440040 400000030020000 1c 3 440000 30000000 18 8000005c 3 0
  //   440000 30000000 80000001c 88000005c 3 104000000000000 2000000000020000 200020 80000040
  //   400000000020000 3 42*0 194000080000040 1800000000458000 428000000460000 1800000030018000
  //   28000000442218 1800000030018000 28000000441118 1800000030018000 440898 30000000 400000418 3
  //   400000000020000 3 0 0 104010088000040 2000000000020000 200000000200000 8020008000000
  //   2000000000020000 200000000200000 8040008000000 2000000000020000 200000000200000 8080008000000
  //   2000000000020000 200000000200000 400000008000000 0 0 0 f000000000 80000040 400000000020000 3 12*0
  //   40000040018000 440000 30000000 80000001c 88000005c 400000000020000 3 13*0 40000040018000 440000
  //   30000000 80000001c 88000005c 400000000020000 3 9*0 40000040018000 440000 30000000 80000001c
  //   88000005c 400000000020000 3 9*0 40000040018000 440000 30000000 80000001c 88000005c 400000000020000 3
  //   5*0 80000040 400000000020000 3 0 80000040 400000000020000 3 9*0 100000000 108100000 108100000
  //   130000000 100880018 80000040 400000000020000 3
  //   ROM_Based_PCU
  //   Ram_A
  //   System_Ram
  //   Ram_B
endmodule

module free_space (
);

  wire [7:0] undriven;

  Counter #(.max('h1f), .width(5)) Program_Counter ();  // open: clr, load, up, count, clk, D, carry, Q
  RAM #(.dataWidth(16)) Instruction_RAM ();  // open: addr, we, oe, clk, din, dout
  RAM #(.dataWidth(16)) ram_1 ();  // open: addr, we, oe, clk, din, dout
  Counter #(.max('h1f), .width(5)) MBR_B_Counter ();  // open: clr, load, up, count, clk, D, carry, Q
  RAM #(.dataWidth(16)) ram_2 ();  // open: addr, we, oe, clk, din, dout
  Counter #(.max('h1f), .width(5)) PCU_part ();  // open: clr, load, up, count, clk, D, carry, Q
  RAM #(.dataWidth(16)) ram_3 ();  // open: addr, we, oe, clk, din, dout
  Counter #(.max('h1f), .width(5)) MBR_A_Counter ();  // open: clr, load, up, count, clk, D, carry, Q
  ROM #(.dataWidth(64)) rom_1 (.addr(undriven));  // open: data

  // Notes on the sheet:
  //   Instruction_Ram
  //   System_Ram
  //   Ram_A
  //   Ram_B
endmodule

module CPU_32 (
);

  wire bus_terminal_32_bit_1_move, bus_terminal_32_bit_1_move_a, bus_terminal_32_bit_1_move_b, clock_1_out,
       controlled_buffer_5_out, controlled_buffer_11_out, controlled_buffer_12_out,
       instruction_splitter_1_flag_or_immediate, not_1_out, not_2_out, not_3_out, not_4_out, not_5_out,
       not_6_out, undriven_2;
  wire [3:0] OPCODE_REGISTER_q_2, Rom_counter_q;
  wire [4:0] controlled_buffer_2_out, controlled_buffer_6_out, controlled_buffer_8_out,
       controlled_buffer_15_out, controlled_buffer_21_out, controlled_buffer_22_out,
       controlled_buffer_31_out, controlled_buffer_33_out, controlled_buffer_35_out, COUNTER_MBR_A_q,
       COUNTER_MBR_B_q, instruction_splitter_1_address_of_a, instruction_splitter_1_adress_of_b,
       instruction_splitter_1_op_code, MAR_A_q, MAR_B_q, MAR_Z_q, Program_counter_main_q;
  wire [4:4] OPCODE_REGISTER_q;
  wire [15:0] controlled_buffer_4_out, controlled_buffer_13_out, INSTRUCTOIN_RAM_dout, MBR_Z_q, undriven_3;
  wire [31:0] A1_q, A2_q, A3_q, A4_q, alu_32_bit_1_answer, alu_32_bit_1_over_flow, alu_register_q, B1_q,
       B2_q, B3_q, B4_q, controlled_buffer_1_out, controlled_buffer_10_out, controlled_buffer_15_out_2,
       controlled_buffer_17_out, controlled_buffer_24_out, controlled_buffer_25_out,
       matrix_muliplication_32_1_out_9, matrix_muliplication_32_1_out_10, matrix_muliplication_32_1_out_11,
       matrix_muliplication_32_1_out_12, MBR_A_q, MBR_B_q, overflow_q, R1_q, ram_1_dout, ram_2_dout,
       ram_3_dout, undriven;
  wire [36:0] bus_terminal_32_bit_1_ram_a, bus_terminal_32_bit_1_ram_b, bus_terminal_32_bit_1_system_ram,
       controlled_buffer_16_out, controlled_buffer_19_out;
  wire [63:0] rom_1_data;

  Counter #(.max('h1f), .width(5)) Program_counter_main (
    .up(rom_1_data[6]), .count(rom_1_data[31]), .clk(clock_1_out), .Q(Program_counter_main_q));  // open: clr, load, D, carry
  // Probe on controlled_buffer_24_out
  // Probe on controlled_buffer_25_out
  Register #(.width(5)) OPCODE_REGISTER (
    .D(instruction_splitter_1_op_code), .en(rom_1_data[14]), .clk(clock_1_out),
    .Q({OPCODE_REGISTER_q[4], OPCODE_REGISTER_q_2}), .clr(rom_1_data[1]));
  // Probe on instruction_splitter_1_op_code
  Register #(.width(32)) alu_register (
    .D(alu_32_bit_1_answer), .en(rom_1_data[2]), .clk(clock_1_out), .Q(alu_register_q));  // open: clr
  ALU_32_bit alu_32_bit_1 (
    .flag(instruction_splitter_1_flag_or_immediate), .A(controlled_buffer_24_out),
    .B(controlled_buffer_25_out), .in_4(OPCODE_REGISTER_q_2), .over_flow(alu_32_bit_1_over_flow),
    .Answer(alu_32_bit_1_answer));
  // Probe on alu_32_bit_1_over_flow
  Register #(.width(32)) A1 (
    .D(controlled_buffer_24_out), .en(rom_1_data[13]), .clk(clock_1_out), .Q(A1_q));  // open: clr
  Register #(.width(32)) B1 (
    .D(controlled_buffer_25_out), .en(rom_1_data[9]), .clk(clock_1_out), .Q(B1_q));  // open: clr
  Register #(.width(32)) B3 (
    .D(controlled_buffer_25_out), .en(rom_1_data[7]), .clk(clock_1_out), .Q(B3_q));  // open: clr
  Register #(.width(32)) overflow (
    .D(alu_32_bit_1_over_flow), .en(rom_1_data[35]), .clk(clock_1_out), .Q(overflow_q));  // open: clr
  Register #(.width(32)) A3 (
    .D(controlled_buffer_24_out), .en(rom_1_data[11]), .clk(clock_1_out), .Q(A3_q));  // open: clr
  assign controlled_buffer_1_out = not_1_out ? alu_register_q : 32'bz;  // Controlled_Buffer controlled_buffer_1
  not not_1 (not_1_out, instruction_splitter_1_flag_or_immediate);
  Register #(.width(32)) A2 (
    .D(controlled_buffer_24_out), .en(rom_1_data[12]), .clk(clock_1_out), .Q(A2_q));  // open: clr
  Register #(.width(32)) A4 (
    .D(controlled_buffer_24_out), .en(rom_1_data[10]), .clk(clock_1_out), .Q(A4_q));  // open: clr
  Register #(.width(32)) B2 (
    .D(controlled_buffer_25_out), .en(rom_1_data[8]), .clk(clock_1_out), .Q(B2_q));  // open: clr
  Register #(.width(32)) B4 (
    .D(controlled_buffer_25_out), .en(rom_1_data[34]), .clk(clock_1_out), .Q(B4_q));  // open: clr
  // Probe on instruction_splitter_1_address_of_a
  assign controlled_buffer_2_out = rom_1_data[56] ? instruction_splitter_1_address_of_a : 5'bz;  // Controlled_Buffer controlled_buffer_2
  assign controlled_buffer_1_out = instruction_splitter_1_flag_or_immediate ? overflow_q : 32'bz;  // Controlled_Buffer controlled_buffer_3
  assign controlled_buffer_4_out = rom_1_data[32] ? MBR_Z_q : 16'bz;  // Controlled_Buffer controlled_buffer_4
  bus_terminal_32_bit bus_terminal_32_bit_1 (
    .op_code({OPCODE_REGISTER_q[4], OPCODE_REGISTER_q_2}), .flag(instruction_splitter_1_flag_or_immediate),
    .address_A(instruction_splitter_1_address_of_a), .data(undriven),
    .addres_B(instruction_splitter_1_adress_of_b), .move_A(bus_terminal_32_bit_1_move_a),
    .move_B(bus_terminal_32_bit_1_move_b), .move(bus_terminal_32_bit_1_move),
    .Ram_A(bus_terminal_32_bit_1_ram_a), .Ram_B(bus_terminal_32_bit_1_ram_b),
    .system_ram(bus_terminal_32_bit_1_system_ram));
  assign controlled_buffer_5_out = rom_1_data[32] ? bus_terminal_32_bit_1_move_a : 1'bz;  // Controlled_Buffer controlled_buffer_5
  assign controlled_buffer_6_out = rom_1_data[61] ? COUNTER_MBR_A_q : 5'bz;  // Controlled_Buffer controlled_buffer_6
  Register #(.width(5)) MAR_Z (
    .D(controlled_buffer_6_out), .en(rom_1_data[17]), .clk(clock_1_out), .Q(MAR_Z_q));  // open: clr
  assign controlled_buffer_6_out = rom_1_data[58] ? Program_counter_main_q : 5'bz;  // Controlled_Buffer controlled_buffer_7
  Register #(.width(5)) MAR_A (
    .D(controlled_buffer_8_out), .en(rom_1_data[16]), .clk(clock_1_out), .Q(MAR_A_q));  // open: clr
  assign controlled_buffer_8_out = undriven_2 ? COUNTER_MBR_A_q : 5'bz;  // Controlled_Buffer controlled_buffer_8
  assign controlled_buffer_8_out = rom_1_data[54] ? instruction_splitter_1_address_of_a : 5'bz;  // Controlled_Buffer controlled_buffer_9
  assign controlled_buffer_10_out = rom_1_data[5] ? controlled_buffer_1_out : 32'bz;  // Controlled_Buffer controlled_buffer_10
  assign controlled_buffer_11_out = rom_1_data[32] ? bus_terminal_32_bit_1_move_b : 1'bz;  // Controlled_Buffer controlled_buffer_11
  assign controlled_buffer_12_out = rom_1_data[32] ? bus_terminal_32_bit_1_move : 1'bz;  // Controlled_Buffer controlled_buffer_12
  // Probe on instruction_splitter_1_adress_of_b
  instruction_splitter instruction_splitter_1 (
    .instruction_full(MBR_Z_q), .wrtite_enable(rom_1_data[26]), .clock(clock_1_out),
    .Adress_of_B(instruction_splitter_1_adress_of_b), .Address_of_A(instruction_splitter_1_address_of_a),
    .op_code(instruction_splitter_1_op_code), .flag_or_immediate(instruction_splitter_1_flag_or_immediate));
  assign controlled_buffer_13_out = rom_1_data[32] ? undriven_3 : 16'bz;  // Controlled_Buffer controlled_buffer_13
  assign controlled_buffer_13_out = rom_1_data[5] ? INSTRUCTOIN_RAM_dout : 16'bz;  // Controlled_Buffer controlled_buffer_14
  not not_2 (not_2_out, controlled_buffer_5_out);
  Pull_Resistor pull_resistor_1 (.node(controlled_buffer_5_out));
  Pull_Resistor pull_resistor_2 (.node(controlled_buffer_12_out));
  assign {controlled_buffer_15_out_2, controlled_buffer_15_out} = rom_1_data[32] ? bus_terminal_32_bit_1_ram_a : 37'bz;  // Controlled_Buffer controlled_buffer_15
  assign controlled_buffer_16_out = rom_1_data[32] ? bus_terminal_32_bit_1_ram_b : 37'bz;  // Controlled_Buffer controlled_buffer_16
  Register #(.width(16)) MBR_Z (
    .D(controlled_buffer_13_out), .en(rom_1_data[27]), .clk(clock_1_out), .Q(MBR_Z_q));  // open: clr
  Register #(.width(32)) MBR_A (
    .D(controlled_buffer_17_out), .en(rom_1_data[28]), .clk(clock_1_out), .Q(MBR_A_q),
    .clr(controlled_buffer_11_out));
  assign controlled_buffer_17_out = not_2_out ? ram_1_dout : 32'bz;  // Controlled_Buffer controlled_buffer_17
  not not_3 (not_3_out, controlled_buffer_11_out);
  assign controlled_buffer_17_out = controlled_buffer_5_out ? controlled_buffer_15_out_2 : 32'bz;  // Controlled_Buffer controlled_buffer_18
  Pull_Resistor pull_resistor_3 (.node(controlled_buffer_11_out));
  Pull_Resistor pull_resistor_4 (.node({controlled_buffer_15_out_2, controlled_buffer_15_out}));
  Pull_Resistor pull_resistor_5 (.node(controlled_buffer_16_out));
  assign controlled_buffer_19_out = rom_1_data[32] ? bus_terminal_32_bit_1_system_ram : 37'bz;  // Controlled_Buffer controlled_buffer_19
  Counter #(.max('h1f), .width(5)) COUNTER_MBR_A (
    .load(rom_1_data[50]), .up(1'b1), .count(rom_1_data[51]), .clk(clock_1_out), .D(controlled_buffer_2_out),
    .Q(COUNTER_MBR_A_q));  // open: clr, carry
  Register #(.width(32)) MBR_B (
    .D(controlled_buffer_16_out[36:5]), .en(rom_1_data[29]), .clk(clock_1_out), .Q(MBR_B_q),
    .clr(controlled_buffer_5_out));
  assign controlled_buffer_16_out[36:5] = not_3_out ? ram_3_dout : 32'bz;  // Controlled_Buffer controlled_buffer_20
  Pull_Resistor pull_resistor_6 (.node(controlled_buffer_19_out));
  Clock clock_1 (.out(clock_1_out));
  assign controlled_buffer_21_out = rom_1_data[55] ? instruction_splitter_1_adress_of_b : 5'bz;  // Controlled_Buffer controlled_buffer_21
  assign controlled_buffer_22_out = rom_1_data[59] ? COUNTER_MBR_B_q : 5'bz;  // Controlled_Buffer controlled_buffer_22
  assign controlled_buffer_22_out = rom_1_data[30] ? instruction_splitter_1_adress_of_b : 5'bz;  // Controlled_Buffer controlled_buffer_23
  Register #(.width(32)) R1 (
    .D(matrix_muliplication_32_1_out_9), .en(rom_1_data[36]), .clk(clock_1_out), .Q(R1_q));  // open: clr
  Register #(.width(32)) R2 (
    .D(matrix_muliplication_32_1_out_10), .en(rom_1_data[37]), .clk(clock_1_out));  // open: Q, clr
  Register #(.width(32)) R3 (
    .D(matrix_muliplication_32_1_out_11), .en(rom_1_data[38]), .clk(clock_1_out));  // open: Q, clr
  matrix_muliplication_32 matrix_muliplication_32_1 (
    .A0(A1_q), .A1(A2_q), .A2(A3_q), .A3(A4_q), .B0(B1_q), .B1(B2_q), .B2(B3_q), .B3(B4_q),
    .out_9(matrix_muliplication_32_1_out_9), .out_10(matrix_muliplication_32_1_out_10),
    .out_11(matrix_muliplication_32_1_out_11), .out_12(matrix_muliplication_32_1_out_12));
  Register #(.width(32)) R4 (
    .D(matrix_muliplication_32_1_out_12), .en(rom_1_data[39]), .clk(clock_1_out));  // open: Q, clr
  assign controlled_buffer_24_out = rom_1_data[4] ? MBR_A_q : 32'bz;  // Controlled_Buffer controlled_buffer_24
  assign controlled_buffer_25_out = rom_1_data[3] ? MBR_B_q : 32'bz;  // Controlled_Buffer controlled_buffer_25
  Register #(.width(5)) MAR_B (
    .D(controlled_buffer_22_out), .en(rom_1_data[15]), .clk(clock_1_out), .Q(MAR_B_q));  // open: clr
  Controlled_Buffer #(.width(16)) controlled_buffer_26 (
    .out(controlled_buffer_13_out), .en(rom_1_data[40]));  // open: in
  Controlled_Buffer #(.width(16)) controlled_buffer_27 (
    .out(controlled_buffer_13_out), .en(rom_1_data[41]));  // open: in
  Controlled_Buffer #(.width(16)) controlled_buffer_28 (
    .out(controlled_buffer_13_out), .en(rom_1_data[42]));  // open: in
  Controlled_Buffer #(.width(16)) controlled_buffer_29 (
    .out(controlled_buffer_13_out), .en(rom_1_data[43]));  // open: in
  Counter #(.max('h1f), .width(5)) COUNTER_MBR_B (
    .load(rom_1_data[52]), .up(1'b1), .count(rom_1_data[53]), .clk(clock_1_out),
    .D(controlled_buffer_21_out), .Q(COUNTER_MBR_B_q));  // open: clr, carry
  Controlled_Buffer #(.width(16)) controlled_buffer_30 (.in(MBR_Z_q), .en(rom_1_data[57]));  // open: out
  assign controlled_buffer_31_out = not_4_out ? MAR_A_q : 5'bz;  // Controlled_Buffer controlled_buffer_31
  not not_4 (not_4_out, controlled_buffer_5_out);
  assign controlled_buffer_31_out = rom_1_data[32] ? controlled_buffer_15_out : 5'bz;  // Controlled_Buffer controlled_buffer_32
  RAM #(.addrWidth(5), .dataWidth(16)) INSTRUCTOIN_RAM (
    .addr(MAR_Z_q), .we(rom_1_data[25]), .oe(rom_1_data[24]), .clk(clock_1_out), .dout(INSTRUCTOIN_RAM_dout));  // open: din
  RAM #(.addrWidth(5), .dataWidth(32)) ram_1 (
    .addr(controlled_buffer_31_out), .we(rom_1_data[23]), .oe(rom_1_data[22]), .clk(clock_1_out),
    .din(controlled_buffer_24_out), .dout(ram_1_dout));
  assign controlled_buffer_33_out = not_5_out ? MAR_Z_q : 5'bz;  // Controlled_Buffer controlled_buffer_33
  not not_5 (not_5_out, controlled_buffer_12_out);
  // Probe on controlled_buffer_10_out
  // Probe on ram_1_dout
  assign controlled_buffer_33_out = rom_1_data[32] ? controlled_buffer_19_out[4:0] : 5'bz;  // Controlled_Buffer controlled_buffer_34
  assign controlled_buffer_35_out = not_6_out ? MAR_B_q : 5'bz;  // Controlled_Buffer controlled_buffer_35
  not not_6 (not_6_out, controlled_buffer_11_out);
  assign controlled_buffer_35_out = rom_1_data[32] ? controlled_buffer_16_out[4:0] : 5'bz;  // Controlled_Buffer controlled_buffer_36
  RAM #(.addrWidth(5), .dataWidth(32)) ram_2 (
    .addr(controlled_buffer_33_out), .we(rom_1_data[21]), .oe(rom_1_data[20]), .clk(clock_1_out),
    .din(controlled_buffer_10_out), .dout(ram_2_dout));
  RAM #(.addrWidth(5), .dataWidth(32)) ram_3 (
    .addr(controlled_buffer_35_out), .we(rom_1_data[19]), .oe(rom_1_data[18]), .clk(clock_1_out),
    .din(controlled_buffer_25_out), .dout(ram_3_dout));
  Counter #(.max('hf), .width(4)) Rom_counter (
    .clr(rom_1_data[0]), .count(1'b1), .clk(clock_1_out), .Q(Rom_counter_q));  // open: load, up, D, carry
  // Probe on ram_3_dout
  ROM #(.dataWidth(64)) rom_1 (.addr({OPCODE_REGISTER_q_2, Rom_counter_q}), .data(rom_1_data));

  // Notes on the sheet:
  //   |
  //   |
  //   |
  //   |
  //   |
  //   |
  //   |
  //   |
  //   |
  //   |
  //   |
  //   ______________
  //   ___________
  //   __________
  //   __________
  //   ___________
  //   __________
  //   _________
  //   __________
  //   ___________
  //   __________
  //   ______________
  //   |
  //   |
  //   |
  //   |
  //   |
  //   |
  //   |
  //   |
  //   |
  //   |
  //   |
  //   |
  //   |
  //   |
  //   |
  //   |
  //   |
  //   |
  //   |
  //   |
  //   |
  //   |
  //   |
  //   |
  //   |
  //   |
  //   |
  //   |
  //   |
  //   |
  //   |
  //   |
  //   |
  //   |
  //   |
  //   |
  //   |
  //   |
  //   |
  //   |
  //   |
  //   |
  //   |
  //   |
  //   |
  //   |
  //   |
  //   |
  //   |
  //   |
  //   |
  //   ___________
  //   __________
  //   ___________
  //   __________
  //   ____________
  //   |
  //   |
  //   |
  //   |
  //   |
  //   |
  //   __________
  //   __
  //   ______________
  //   ______________
  //   ______________
  //   __
  //   __
  //   __
  //   __
  //   __
  //   __
  //   __
  //   __
  //   __
  //   __
  //   __
  //   __
  //   __
  //   __
  //   __
  //   __
  //   __
  //   __
  //   __
  //   __
  //   __
  //   __
  //   __
  //   __
  //   __
  //   __
  //   __
  //   __
  //   __
  //   __
  //   __
  //   __
  //   __
  //   __
  //   __
  //   __
  //   __
  //   __
  //   __
  //   __
  //   __
  //   __
  //   __
  //   __
  //   __
  //   __
  //   __
  //   __
  //   __
  //   __
  //   __
  //   __
  //   __
  //   __
  //   __
  //   __
  //   __
  //   __
  //   __
  //   __
  //   __
  //   __
  //   __
  //   __
  //   __
  //   __
  //   __
  //   __
  //   __
  //   __
  //   __
  //   __
  //   __
  //   __
  //   __
  //   __
  //   __
  //   __
  //   __
  //   __
  //   __
  //   __
  //   __
  //   __
  //   __
  //   __
  //   __
  //   __
  //   __
  //   __
  //   __
  //   __
  //   __
  //   __
  //   __
  //   __
  //   __
  //   __
  //   __
  //   __
  //   __
  //   __
  //   __
  //   __
  //   __
  //   __
  //   __
  //   __
  //   __
  //   __
  //   __
  //   __
  //   __
  //   __
  //   __
  //   __
  //   __
  //   __
  //   __
  //   __
  //   __
  //   __
  //   __
  //   __
  //   __
  //   __
  //   __
  //   __
  //   __
  //   __
  //   __
  //   __
  //   __
  //   __
  //   __
  //   __
  //   __
  //   __
  //   __
  //   __
  //   __
  //   __
  //   __
  //   __
  //   __
  //   __
  //   __
  //   __
  //   __
  //   __
  //   __
  //   __
  //   __
  //   __
  //   __
  //   __
  //   __
  //   __
  //   __
  //   __
  //   __
  //   __
  //   __
  //   __
  //   __
  //   __
  //   __
  //   __
  //   __
  //   __
  //   __
  //   __
  //   __
  //   __
  //   |
  //   |
  //   |
  //   |
  //   |
  //   |
  //   ___________
  //   __________
  //   __________
  //   __________
  //   |
  //   __
  //   __
  //   __
  //   __
  //   __
  //   __
  //   __
  //   __
  //   __
  //   __
  //   __
  //   __
  //   __
  //   __
  //   __
  //   __
  //   __
  //   __
  //   __
  //   __
  //   __
  //   __
  //   __
  //   __
  //   __
  //   __
  //   __
  //   __
  //   __
  //   __
  //   __
  //   __
  //   |
  //   |
  //   |
  //   |
  //   |
  //   |
  //   |
  //   |
  //   |
  //   __
  //   __
  //   __
  //   __
  //   __
  //   __
  //   |
  //   |
  //   |
  //   |
  //   |
  //   |
  //   |
  //   |
  //   |
  //   |
  //   |
  //   |
  //   ____
  //   ____
  //   __
  //   __
  //   __
  //   __
  //   __
  //   __
  //   __
  //   __
  //   __
  //   __
  //   __
  //   __
  //   __
  //   __
  //   __
  //   __
  //   __
  //   __
  //   __
  //   __
  //   __
  //   __
  //   __
  //   __
  //   __
  //   __
  //   __
  //   __
  //   __
  //   __
  //   __
  //   __
  //   __
  //   __
  //   __
  //   __
  //   __
  //   __
  //   __
  //   __
  //   __
  //   __
  //   __
  //   __
  //   __
  //   __
  //   __
  //   __
  //   __
  //   __
  //   __
  //   __
  //   __
  //   __
  //   __
  //   __
  //   __
  //   __
  //   __
  //   __
  //   __
  //   __
  //   __
  //   __
  //   __
  //   __
  //   __
  //   __
  //   __
  //   __
  //   __
  //   __
  //   __
  //   __
  //   __
  //   __
  //   __
  //   __
  //   __
  //   __
  //   __
  //   __
  //   __
  //   __
  //   __
  //   __
  //   __
  //   __
  //   __
  //   __
  //   __
  //   __
  //   __
  //   __
  //   __
  //   __
  //   __
  //   __
  //   __
  //   __
  //   __
  //   __
  //   __
  //   __
  //   __
  //   __
  //   __
  //   __
  //   __
  //   __
  //   __
  //   __
  //   __
  //   __
  //   __
  //   __
  //   __
  //   __
  //   __
  //   __
  //   __
  //   __
  //   __
  //   __
  //   __
  //   __
  //   __
  //   __
  //   __
  //   __
  //   __
  //   __
  //   __
  //   __
  //   __
  //   __
  //   __
  //   __
  //   __
  //   __
  //   __
  //   __
  //   __
  //   __
  //   __
  //   __
  //   __
  //   __
  //   __
  //   __
  //   __
  //   __
  //   __
  //   __
  //   __
  //   __
  //   __
  //   __
  //   __
  //   __
  //   __
  //   __
  //   __
  //   __
  //   __
  //   __
  //   __
  //   __
  //   __
  //   __
  //   __
  //   __
  //   __
  //   __
  //   __
  //   __
  //   __
  //   __
  //   __
  //   __
  //   __
  //   __
  //   __
  //   __
  //   __
  //   __
  //   __
  //   __
  //   __
  //   __
  //   __
  //   __
  //   __
  //   __
  //   __
  //   __
  //   __
  //   __
  //   __
  //   __
  //   __
  //   __
  //   __
  //   __
  //   __
  //   __
  //   __
  //   __
  //   __
  //   __
  //   __
  //   __
  //   __
  //   __
  //   __
  //   __
  //   __
  //   __
  //   __
  //   __
  //   __
  //   __
  //   __
  //   __
  //   __
  //   __
  //   __
  //   __
  //   __
  //   __
  //   __
  //   __
  //   __
  //   __
  //   __
  //   __
  //   __
  //   __
  //   __
  //   __
  //   __
  //   __
  //   __
  //   __
  //   __
  //   __
  //   __
  //   __
  //   __
  //   __
  //   __
  //   __
  //   __
  //   __
  //   __
  //   __
  //   __
  //   __
  //   __
  //   __
  //   __
  //   __
  //   __
  //   __
  //   __
  //   __
  //   __
  //   __
  //   __
  //   __
  //   __
  //   __
  //   __
  //   __
  //   __
  //   __
  //   __
  //   __
  //   __
  //   __
  //   __
  //   __
  //   __
  //   __
  //   __
  //   __
  //   __
  //   __
  //   __
  //   __
  //   __
  //   __
  //   __
  //   __
  //   __
  //   __
  //   __
  //   __
  //   __
  //   __
  //   __
  //   __
  //   __
  //   __
  //   __
  //   __
  //   __
  //   __
  //   __
  //   __
  //   __
  //   __
  //   __
  //   __
  //   __
  //   __
  //   __
  //   __
  //   __
  //   __
  //   __
  //   __
  //   __
  //   __
  //   __
  //   __
  //   __
  //   __
  //   __
  //   __
  //   __
  //   __
  //   __
  //   __
  //   __
  //   __
  //   __
  //   __
  //   __
  //   __
  //   __
  //   __
  //   __
  //   __
  //   __
  //   __
  //   __
  //   __
  //   __
  //   __
  //   __
  //   __
  //   __
  //   __
  //   __
  //   __
  //   __
  //   __
  //   __
  //   __
  //   __
  //   __
  //   __
  //   __
  //   __
  //   __
  //   __
  //   __
  //   __
  //   __
  //   __
  //   __
  //   __
  //   __
  //   __
  //   __
  //   __
  //   __
  //   __
  //   __
  //   __
  //   __
  //   __
  //   __
  //   __
  //   __
  //   __
  //   __
  //   __
  //   __
  //   __
  //   __
  //   __
  //   __
  //   __
  //   __
  //   __
  //   __
  //   __
  //   __
  //   __
  //   __
  //   __
  //   __
  //   __
  //   __
  //   __
  //   __
  //   __
  //   __
  //   __
  //   __
  //   __
  //   __
  //   __
  //   __
  //   __
  //   __
  //   __
  //   __
  //   __
  //   __
  //   __
  //   __
  //   __
  //   __
  //   __
  //   __
  //   __
  //   __
  //   __
  //   __
  //   __
  //   __
  //   __
  //   __
  //   __
  //   __
  //   __
  //   __
  //   __
  //   __
  //   __
  //   __
  //   __
  //   __
  //   __
  //   __
  //   __
  //   __
  //   __
  //   __
  //   __
  //   __
  //   __
  //   __
  //   __
  //   __
  //   __
  //   __
  //   __
  //   __
  //   __
  //   __
  //   __
  //   __
  //   __
  //   __
  //   __
  //   __
  //   __
  //   __
  //   __
  //   __
  //   __
  //   __
  //   __
  //   __
  //   __
  //   __
  //   __
  //   __
  //   __
  //   __
  //   __
  //   __
  //   __
  //   __
  //   __
  //   __
  //   __
  //   __
  //   __
  //   __
  //   __
  //   __
  //   __
  //   __
  //   __
  //   __
  //   __
  //   __
  //   __
  //   __
  //   __
  //   __
  //   __
  //   __
  //   __
  //   __
  //   __
  //   __
  //   __
  //   __
  //   __
  //   __
  //   __
  //   __
  //   __
  //   __
  //   __
  //   __
  //   __
  //   __
  //   __
  //   __
  //   __
  //   __
  //   __
  //   __
  //   __
  //   __
  //   __
  //   __
  //   __
  //   __
  //   __
  //   __
  //   __
  //   __
  //   __
  //   __
  //   __
  //   __
  //   __
  //   __
  //   __
  //   __
  //   __
  //   __
  //   __
  //   __
  //   __
  //   __
  //   __
  //   __
  //   __
  //   __
  //   __
  //   __
  //   __
  //   __
  //   __
  //   __
  //   __
  //   __
  //   __
  //   __
  //   __
  //   __
  //   __
  //   __
  //   __
  //   __
  //   __
  //   __
  //   __
  //   __
  //   __
  //   __
  //   __
  //   __
  //   __
  //   __
  //   __
  //   __
  //   __
  //   __
  //   __
  //   __
  //   __
  //   __
  //   __
  //   __
  //   __
  //   __
  //   __
  //   __
  //   __
  //   __
  //   __
  //   __
  //   __
  //   __
  //   __
  //   __
  //   __
  //   __
  //   __
  //   __
  //   __
  //   __
  //   __
  //   __
  //   __
  //   __
  //   __
  //   __
  //   __
  //   __
  //   __
  //   __
  //   __
  //   __
  //   __
  //   __
  //   __
  //   __
  //   __
  //   __
  //   __
  //   __
  //   __
  //   __
  //   __
  //   __
  //   __
  //   __
  //   __
  //   __
  //   __
  //   __
  //   __
  //   __
  //   __
  //   __
  //   __
  //   __
  //   __
  //   __
  //   __
  //   __
  //   O
  //   __
  //   __
  //   __
  //   __
  //   __
  //   __
  //   __
  //   __
  //   __
  //   __
  //   __
  //   __
  //   __
  //   __
  //   __
  //   __
  //   __
  //   __
  //   __
  //   __
  //   __
  //   __
  //   __
  //   __
  //   __
  //   __
  //   __
  //   __
  //   __
  //   __
  //   __
  //   __
  //   __
  //   __
  //   __
  //   __
  //   __
  //   __
  //   __
  //   __
  //   __
  //   __
  //   __
  //   __
  //   __
  //   __
  //   __
  //   __
  //   __
  //   __
  //   __
  //   __
  //   __
  //   __
  //   __
  //   __
  //   __
  //   __
  //   __
  //   __
  //   __
  //   __
  //   __
  //   __
  //   __
  //   __
  //   __
  //   __
  //   __
  //   __
  //   __
  //   __
  //   __
  //   __
  //   __
  //   __
  //   __
  //   __
  //   __
  //   __
  //   __
  //   __
  //   __
  //   __
  //   __
  //   __
  //   __
  //   __
  //   __
  //   __
  //   __
  //   __
  //   __
  //   __
  //   __
  //   __
  //   __
  //   __
  //   __
  //   __
  //   __
  //   __
  //   __
  //   __
  //   __
  //   __
  //   __
  //   __
  //   __
  //   __
  //   __
  //   __
  //   __
  //   __
  //   __
  //   __
  //   __
  //   __
  //   __
  //   __
  //   __
  //   __
  //   __
  //   __
  //   __
  //   __
  //   __
  //   __
  //   __
  //   __
  //   __
  //   __
  //   __
  //   __
  //   __
  //   __
  //   __
  //   __
  //   __
  //   __
  //   __
  //   __
  //   __
  //   __
  //   __
  //   __
  //   __
  //   __
  //   __
  //   __
  //   __
  //   __
  //   __
  //   __
  //   __
  //   __
  //   __
  //   __
  //   __
  //   __
  //   __
  //   __
  //   __
  //   __
  //   __
  //   __
  //   __
  //   __
  //   __
  //   __
  //   __
  //   __
  //   __
  //   __
  //   __
  //   __
  //   __
  //   __
  //   __
  //   __
  //   __
  //   __
  //   __
  //   __
  //   __
  //   __
  //   __
  //   __
  //   __
  //   __
  //   __
  //   __
  //   __
  //   __
  //   __
  //   __
  //   __
  //   __
  //   __
  //   __
  //   __
  //   __
  //   __
  //   __
  //   __
  //   __
  //   __
  //   __
  //   __
  //   __
  //   __
  //   __
  //   __
  //   __
  //   __
  //   __
  //   __
  //   __
  //   __
  //   __
  //   __
  //   __
  //   __
  //   __
  //   __
  //   __
  //   __
  //   __
  //   __
  //   __
  //   __
  //   __
  //   __
  //   __
  //   __
  //   __
  //   __
  //   __
  //   __
  //   __
  //   __
  //   __
  //   __
  //   __
  //   __
  //   __
  //   __
  //   __
  //   __
  //   __
  //   __
  //   __
  //   __
  //   __
  //   __
  //   __
  //   __
  //   __
  //   __
  //   __
  //   __
  //   __
  //   __
  //   __
  //   __
  //   __
  //   __
  //   __
  //   __
  //   __
  //   __
  //   __
  //   __
  //   __
  //   __
  //   __
  //   __
  //   __
  //   __
  //   __
  //   __
  //   __
  //   __
  //   __
  //   __
  //   __
  //   __
  //   __
  //   __
  //   __
  //   __
  //   __
  //   __
  //   __
  //   __
  //   __
  //   __
  //   __
  //   __
  //   __
  //   __
  //   __
  //   __
  //   __
  //   __
  //   __
  //   __
  //   __
  //   __
  //   __
  //   __
  //   __
  //   __
  //   __
  //   __
  //   __
  //   __
  //   __
  //   __
  //   __
  //   __
  //   __
  //   __
  //   __
  //   __
  //   __
  //   __
  //   __
  //   __
  //   __
  //   __
  //   __
  //   __
  //   __
  //   __
  //   __
  //   __
  //   __
  //   __
  //   __
  //   __
  //   __
  //   __
  //   __
  //   __
  //   __
  //   __
  //   __
  //   __
  //   __
  //   __
  //   __
  //   __
  //   __
  //   __
  //   __
  //   __
  //   __
  //   __
  //   __
  //   __
  //   __
  //   __
  //   __
  //   __
  //   __
  //   __
  //   __
  //   __
  //   __
  //   __
  //   __
  //   __
  //   __
  //   __
  //   __
  //   __
  //   __
  //   __
  //   __
  //   __
  //   __
  //   __
  //   __
  //   __
  //   __
  //   __
  //   __
  //   __
  //   __
  //   __
  //   __
  //   __
  //   __
  //   __
  //   __
  //   __
  //   __
  //   __
  //   __
  //   __
  //   __
  //   __
  //   __
  //   __
  //   __
  //   __
  //   __
  //   __
  //   __
  //   __
  //   __
  //   __
  //   __
  //   __
  //   __
  //   __
  //   __
  //   __
  //   __
  //   __
  //   __
  //   __
  //   __
  //   __
  //   __
  //   __
  //   __
  //   __
  //   __
  //   __
  //   __
  //   __
  //   __
  //   __
  //   __
  //   __
  //   __
  //   __
  //   __
  //   __
  //   __
  //   __
  //   __
  //   __
  //   __
  //   __
  //   __
  //   __
  //   __
  //   __
  //   __
  //   __
  //   __
  //   __
  //   __
  //   __
  //   __
  //   __
  //   __
  //   __
  //   __
  //   __
  //   __
  //   __
  //   __
  //   __
  //   __
  //   __
  //   __
  //   __
  //   __
  //   __
  //   __
  //   __
  //   __
  //   __
  //   __
  //   __
  //   __
  //   __
  //   __
  //   __
  //   __
  //   __
  //   __
  //   __
  //   __
  //   __
  //   __
  //   __
  //   __
  //   __
  //   __
  //   __
  //   __
  //   __
  //   __
  //   __
  //   __
  //   __
  //   __
  //   __
  //   __
  //   __
  //   __
  //   __
  //   __
  //   __
  //   __
  //   __
  //   __
  //   __
  //   __
  //   __
  //   __
  //   __
  //   __
  //   __
  //   __
  //   __
  //   __
  //   __
  //   __
  //   __
  //   __
  //   __
  //   __
  //   __
  //   __
  //   __
  //   __
  //   __
  //   __
  //   __
  //   __
  //   __
  //   __
  //   __
  //   __
  //   __
  //   __
  //   __
  //   __
  //   __
  //   __
  //   __
  //   __
  //   __
  //   __
  //   __
  //   __
  //   __
  //   __
  //   __
  //   __
  //   __
  //   __
  //   __
  //   Instruction_RAM
  //   RAM_A
  //   System_RAM
  //   RAM_B
  //   contents of rom_1 (hex, n*v repeats v):
  //   400000001020000 8000020 4018020 4000 16*0 40000040018000 440000 30000000 80000001c 88000005c
  //   400000000020000 3 25*0 40000040018000 80440040 400000030020000 1c 3 440000 30000000 18 8000005c 3 0
  //   440000 30000000 80000001c 88000005c 3 104000000000000 2000000000020000 200020 80000040
  //   400000000020000 3 42*0 194000080000040 1800000000458000 428000000460000 1800000030018000
  //   28000000442218 1800000030018000 28000000441118 1800000030018000 440898 30000000 400000418 3
  //   400000000020000 3 0 0 104010088000040 2000000000020000 200000000200000 8020008000000
  //   2000000000020000 200000000200000 8040008000000 2000000000020000 200000000200000 8080008000000
  //   2000000000020000 200000000200000 400000008000000 0 0 0 f000000000 80000040 400000000020000 3 12*0
  //   40000040018000 440000 30000000 80000001c 88000005c 400000000020000 3 13*0 40000040018000 440000
  //   30000000 80000001c 88000005c 400000000020000 3 9*0 40000040018000 440000 30000000 80000001c
  //   88000005c 400000000020000 3 9*0 40000040018000 440000 30000000 80000001c 88000005c 400000000020000 3
  //   5*0 80000040 400000000020000 3 0 80000040 400000000020000 3 9*0 100000000 108100000 108100000
  //   130000000 100880018 80000040 400000000020000 3
  //   ROM_Based_PCU
endmodule
